// Digital circuit 02.dig as structural Verilog
module _02 (
  input  [2:0] in1,
  input  [2:0] in0,
  input  addsubtract,
  output [2:0] out
);

  wire and_1_out, and_2_out, and_3_out, and_4_out, and_5_out, and_6_out, and_7_out, and_8_out, and_9_out,
       and_10_out, and_11_out, and_12_out, and_13_out, and_14_out, and_15_out, and_16_out, and_17_out,
       and_18_out, and_19_out, and_20_out, and_21_out, and_22_out, and_23_out, and_24_out, and_25_out,
       and_26_out, and_27_out, and_28_out, and_29_out, and_30_out, and_31_out, and_32_out, and_33_out,
       and_34_out, and_35_out, and_36_out, and_37_out, and_38_out, and_39_out, and_40_out, and_41_out,
       and_42_out, and_43_out, and_44_out, and_45_out, and_46_out, and_47_out, and_48_out, and_49_out,
       and_50_out, and_51_out, and_52_out, and_53_out, and_54_out, and_55_out, and_56_out, and_57_out,
       and_58_out, and_59_out, and_60_out, and_61_out, and_62_out, and_63_out, and_64_out, and_65_out,
       and_66_out, and_67_out, and_68_out, and_69_out, and_70_out, and_71_out, and_72_out, and_73_out,
       and_74_out, and_75_out, and_76_out, and_77_out, and_78_out, and_79_out, and_80_out, and_81_out,
       not_1_out, not_2_out, not_3_out, not_4_out, not_5_out, not_6_out, not_7_out;

  not not_1 (not_1_out, in1[2]);
  not not_2 (not_2_out, in1[1]);
  not not_3 (not_3_out, in1[0]);
  not not_4 (not_4_out, in0[2]);
  not not_5 (not_5_out, in0[1]);
  not not_6 (not_6_out, in0[0]);
  not not_7 (not_7_out, addsubtract);
  and and_1 (and_1_out, not_7_out, in0[0], in0[1], in0[2], in1[0]);
  and and_2 (and_2_out, not_7_out, in0[0], in0[1], in0[2], in1[1]);
  and and_3 (and_3_out, not_7_out, in0[0], in0[1], in0[2], in1[2]);
  and and_4 (and_4_out, not_7_out, in0[0], in0[1], in1[0], in1[1]);
  and and_5 (and_5_out, not_7_out, in0[0], in0[1], in1[0], in1[2]);
  and and_6 (and_6_out, not_7_out, in0[0], in0[1], in1[1], in1[2]);
  and and_7 (and_7_out, not_7_out, in0[0], in0[2], in1[0], in1[1]);
  and and_8 (and_8_out, not_7_out, in0[0], in0[2], in1[0], in1[2]);
  and and_9 (and_9_out, not_7_out, in0[0], in0[2], in1[1], in1[2]);
  and and_10 (and_10_out, not_7_out, in0[0], in1[0], in1[1], in1[2]);
  and and_11 (and_11_out, not_7_out, in0[1], in0[2], in1[0], in1[1]);
  and and_12 (and_12_out, not_7_out, in0[1], in0[2], in1[0], in1[2]);
  and and_13 (and_13_out, not_7_out, in0[1], in0[2], in1[1], in1[2]);
  and and_14 (and_14_out, not_7_out, in0[1], in1[0], in1[1], in1[2]);
  and and_15 (and_15_out, not_7_out, in0[2], in1[0], in1[1], in1[2]);
  and and_16 (and_16_out, not_7_out, in0[0], not_5_out, not_4_out, in1[0], not_2_out);
  and and_17 (and_17_out, not_7_out, not_6_out, in0[1], not_4_out, in1[0], not_2_out);
  and and_18 (and_18_out, not_7_out, in0[0], not_5_out, not_4_out, not_3_out, in1[1]);
  and and_19 (and_19_out, not_7_out, not_6_out, in0[1], not_4_out, not_3_out, in1[1]);
  and and_20 (and_20_out, not_7_out, in0[0], not_5_out, not_3_out, not_2_out, in1[2]);
  and and_21 (and_21_out, not_7_out, not_6_out, in0[1], not_3_out, not_2_out, in1[2]);
  and and_22 (and_22_out, not_7_out, not_6_out, in0[2], in1[0], not_2_out, not_1_out);
  and and_23 (and_23_out, not_7_out, not_6_out, in0[2], not_3_out, in1[1], not_1_out);
  and and_24 (and_24_out, addsubtract, not_6_out, not_4_out, in1[0], in1[1]);
  and and_25 (and_25_out, addsubtract, not_5_out, not_4_out, in1[0], in1[1]);
  and and_26 (and_26_out, not_7_out, in0[0], in0[1], in0[2], in1[0], in1[1], in1[2]);
  and and_27 (and_27_out, addsubtract, in0[0], in0[1], in0[2], not_3_out, not_2_out);
  and and_28 (and_28_out, addsubtract, in0[0], in0[1], in0[2], not_3_out, not_1_out);
  and and_29 (and_29_out, not_7_out, in0[0], not_5_out, not_4_out, in1[0], not_1_out);
  and and_30 (and_30_out, not_7_out, not_6_out, in0[1], not_4_out, in1[0], not_1_out);
  and and_31 (and_31_out, not_7_out, not_6_out, not_5_out, in0[2], not_3_out, in1[2]);
  and and_32 (and_32_out, addsubtract, in0[0], in0[1], in0[2], not_2_out, not_1_out);
  and and_33 (and_33_out, not_7_out, in0[0], not_5_out, in1[0], not_2_out, not_1_out);
  and and_34 (and_34_out, not_7_out, in0[0], not_5_out, not_3_out, in1[1], not_1_out);
  and and_35 (and_35_out, not_7_out, in0[0], not_4_out, in1[0], not_2_out, not_1_out);
  and and_36 (and_36_out, not_7_out, in0[0], not_4_out, not_3_out, in1[1], not_1_out);
  and and_37 (and_37_out, not_7_out, in0[0], not_4_out, not_3_out, not_2_out, in1[2]);
  and and_38 (and_38_out, addsubtract, not_6_out, not_5_out, in1[0], in1[1]);
  and and_39 (and_39_out, addsubtract, not_6_out, not_4_out, in1[0], in1[2]);
  and and_40 (and_40_out, addsubtract, not_6_out, not_4_out, in1[1], in1[2]);
  and and_41 (and_41_out, addsubtract, not_5_out, not_4_out, in1[0], in1[2]);
  and and_42 (and_42_out, addsubtract, not_5_out, not_4_out, in1[1], in1[2]);
  and and_43 (and_43_out, not_6_out, not_5_out, in1[0], in1[1], not_1_out);
  and and_44 (and_44_out, not_6_out, not_5_out, in1[0], not_2_out, in1[2]);
  and and_45 (and_45_out, not_6_out, not_5_out, not_3_out, in1[1], in1[2]);
  and and_46 (and_46_out, not_6_out, not_5_out, not_4_out, in1[0], in1[1]);
  and and_47 (and_47_out, in0[0], in0[1], not_3_out, not_2_out, not_1_out);
  and and_48 (and_48_out, in0[0], in0[2], not_3_out, not_2_out, not_1_out);
  and and_49 (and_49_out, in0[1], in0[2], not_3_out, not_2_out, not_1_out);
  and and_50 (and_50_out, in0[0], not_5_out, not_4_out, not_3_out, not_2_out, not_1_out);
  and and_51 (and_51_out, not_6_out, in0[1], not_4_out, not_3_out, not_2_out, not_1_out);
  and and_52 (and_52_out, not_6_out, not_5_out, in0[2], not_3_out, not_2_out, not_1_out);
  and and_53 (and_53_out, in0[0], in0[1], in0[2], not_3_out, not_2_out, not_1_out);
  and and_54 (and_54_out, not_6_out, not_5_out, not_4_out, in1[0], not_2_out, not_1_out);
  and and_55 (and_55_out, in0[0], in0[1], not_4_out, in1[0], not_2_out, not_1_out);
  and and_56 (and_56_out, in0[0], not_5_out, in0[2], in1[0], not_2_out, not_1_out);
  and and_57 (and_57_out, not_6_out, in0[1], in0[2], in1[0], not_2_out, not_1_out);
  and and_58 (and_58_out, not_6_out, not_5_out, not_4_out, not_3_out, in1[1], not_1_out);
  and and_59 (and_59_out, in0[0], in0[1], not_4_out, not_3_out, in1[1], not_1_out);
  and and_60 (and_60_out, in0[0], not_5_out, in0[2], not_3_out, in1[1], not_1_out);
  and and_61 (and_61_out, not_6_out, in0[1], in0[2], not_3_out, in1[1], not_1_out);
  and and_62 (and_62_out, in0[0], not_5_out, not_4_out, in1[0], in1[1], not_1_out);
  and and_63 (and_63_out, not_6_out, in0[1], not_4_out, in1[0], in1[1], not_1_out);
  and and_64 (and_64_out, not_6_out, not_5_out, in0[2], in1[0], in1[1], not_1_out);
  and and_65 (and_65_out, in0[0], in0[1], in0[2], in1[0], in1[1], not_1_out);
  and and_66 (and_66_out, not_6_out, not_5_out, not_4_out, not_3_out, not_2_out, in1[2]);
  and and_67 (and_67_out, in0[0], in0[1], not_4_out, not_3_out, not_2_out, in1[2]);
  and and_68 (and_68_out, in0[0], not_5_out, in0[2], not_3_out, not_2_out, in1[2]);
  and and_69 (and_69_out, not_6_out, in0[1], in0[2], not_3_out, not_2_out, in1[2]);
  and and_70 (and_70_out, in0[0], not_5_out, not_4_out, in1[0], not_2_out, in1[2]);
  and and_71 (and_71_out, not_6_out, in0[1], not_4_out, in1[0], not_2_out, in1[2]);
  and and_72 (and_72_out, not_6_out, not_5_out, in0[2], in1[0], not_2_out, in1[2]);
  and and_73 (and_73_out, in0[0], in0[1], in0[2], in1[0], not_2_out, in1[2]);
  and and_74 (and_74_out, in0[0], not_5_out, not_4_out, not_3_out, in1[1], in1[2]);
  and and_75 (and_75_out, not_6_out, in0[1], not_4_out, not_3_out, in1[1], in1[2]);
  and and_76 (and_76_out, not_6_out, not_5_out, in0[2], not_3_out, in1[1], in1[2]);
  and and_77 (and_77_out, in0[0], in0[1], in0[2], not_3_out, in1[1], in1[2]);
  and and_78 (and_78_out, not_6_out, not_5_out, not_4_out, in1[0], in1[1], in1[2]);
  and and_79 (and_79_out, in0[0], in0[1], not_4_out, in1[0], in1[1], in1[2]);
  and and_80 (and_80_out, in0[0], not_5_out, in0[2], in1[0], in1[1], in1[2]);
  and and_81 (and_81_out, not_6_out, in0[1], in0[2], in1[0], in1[1], in1[2]);
  or or_1 (out[2], and_1_out, and_2_out, and_3_out, and_4_out, and_5_out, and_6_out, and_7_out, and_8_out, and_9_out, and_10_out, and_11_out, and_12_out, and_13_out, and_14_out, and_15_out);
  or or_2 (out[1], and_16_out, and_17_out, and_18_out, and_19_out, and_20_out, and_21_out, and_22_out, and_23_out, and_24_out, and_25_out, and_26_out, and_27_out, and_28_out, and_29_out, and_30_out, and_31_out, and_32_out, and_33_out, and_34_out, and_35_out, and_36_out, and_37_out, and_38_out, and_39_out, and_40_out, and_41_out, and_42_out, and_43_out, and_44_out, and_45_out, and_46_out, and_47_out, and_48_out, and_49_out);
  or or_3 (out[0], and_50_out, and_51_out, and_52_out, and_53_out, and_54_out, and_55_out, and_56_out, and_57_out, and_58_out, and_59_out, and_60_out, and_61_out, and_62_out, and_63_out, and_64_out, and_65_out, and_66_out, and_67_out, and_68_out, and_69_out, and_70_out, and_71_out, and_72_out, and_73_out, and_74_out, and_75_out, and_76_out, and_77_out, and_78_out, and_79_out, and_80_out, and_81_out);

  // Other names for the same wires on the sheet: in0_0 = in0[0]; in0_1 = in0[1]; in0_2 = in0[2]; in1_0 = in1[0];
  //   in1_1 = in1[1]; in1_2 = in1[2]; out_0 = out[0]; out_1 = out[1]; out_2 = out[2]
endmodule
