// Digital circuit 02.dig as structural Verilog
module _02 (
  input  [31:0] A,
  input  \input ,
  input  clk,
  input  in_6,
  input  reset,
  output [7:0] sqrt,
  output busy,
  output less
);

  wire _00, _01, _02, _03, equal, morethan, multiplexer_1_out, multiplexer_2_out, or_1_out, or_2_out, Q1;
  wire [0:0] Q1_plus_2;
  wire [31:0] count, multiplexer_3_out, sub_1_s;
  wire [31:8] register_1_q;
  wire [63:0] check;

  or or_1 (or_1_out, morethan, equal);
  Multiplexer #(.Selector_Bits(2)) multiplexer_1 (
    .sel({Q1, Q1_plus_2[0]}), .in_0(1'b0), .in_1(1'b1), .in_2(or_1_out), .in_3(1'b0), .out(multiplexer_1_out));
  D_FF d_ff_1 (.D(multiplexer_1_out), .C(clk), .Q(Q1));  // open: nQ
  or or_2 (or_2_out, morethan, equal);
  Counter #(.Bits(32)) counter_1 (.en(_02), .C(clk), .clr(reset), .out(count));  // open: ovf
  Multiplexer #(.Selector_Bits(2)) multiplexer_2 (
    .sel({Q1, Q1_plus_2[0]}), .in_0(\input ), .in_1(or_2_out), .in_2(1'b1), .in_3(1'b0),
    .out(multiplexer_2_out));
  D_FF d_ff_2 (.D(multiplexer_2_out), .C(clk), .Q(Q1_plus_2[0]));  // open: nQ
  Comparator #(.Bits(32)) comparator_1 (.a(check[31:0]), .b(A), .gt(morethan), .eq(equal), .lt(less));
  Decoder #(.Selector_Bits(2)) decoder_1 (.sel({Q1, Q1_plus_2[0]}), .out_0(_00), .out_1(_01), .out_2(_02), .out_3(_03));
  Mul #(.Bits(32)) mul_1 (.a(count), .b(count), .mul(check));
  Sub #(.Bits(32)) sub_1 (.a(count), .b(32'h1), .c_i(1'b0), .s(sub_1_s));  // open: c_o
  Multiplexer #(.Bits(32)) multiplexer_3 (.sel(morethan), .in_0(count), .in_1(sub_1_s), .out(multiplexer_3_out));
  Register #(.Bits(32)) register_1 (.D(multiplexer_3_out), .C(clk), .en(_03), .Q({register_1_q, sqrt}));

  assign busy = in_6;

  // Other names for the same wires on the sheet: Q1_plus_2[1] = Q1; Q2 = Q1_plus_2[0]

  // Notes on the sheet:
  //   clk: Hz: 50
endmodule

/* Test case TestCase1:
clk A input sqrt busy
0 0 0 0 0
1 0 0 0 0
0 0 0 0 0
1 0 0 0 0
0 0 1 X X
1 0 1 X X
loop(x,1000)
0 0 0 X X
1 0 0 X X
end loop
0 0 0 0 0
1 0 0 0 0
*/

/* Test case TestCase2:
clk A input sqrt busy
0 0 0 0 0
1 0 0 0 0
0 0 0 0 0
1 0 0 0 0
0 1 1 X X
1 1 1 X X
loop(x,1000)
0 1 0 X X
1 1 0 X X
end loop
0 0 0 1 0
1 0 0 1 0
*/

/* Test case TestCase3:
clk A input sqrt busy
0 0 0 0 0
1 0 0 0 0
0 0 0 0 0
1 0 0 0 0
0 4 1 X X
1 4 1 X X
loop(x,1000)
0 4 0 X X
1 4 0 X X
end loop
0 0 0 2 0
1 0 0 2 0
*/

/* Test case TestCase4:
clk A input sqrt busy
0 0 0 0 0
1 0 0 0 0
0 0 0 0 0
1 0 0 0 0
0 9 1 X X
1 9 1 X X
loop(x,1000)
0 9 0 X X
1 9 0 X X
end loop
0 0 0 3 0
1 0 0 3 0
*/

/* Test case TestCase5:
clk A input sqrt busy
0 0 0 0 0
1 0 0 0 0
0 0 0 0 0
1 0 0 0 0
0 8 1 X X
1 8 1 X X
loop(x,1000)
0 8 0 X X
1 8 0 X X
end loop
0 0 0 2 0
1 0 0 2 0
*/

/* Test case TestCase6:
clk A input sqrt busy
0 0 0 0 0
1 0 0 0 0
0 0 0 0 0
1 0 0 0 0
0 65536 1 X X
1 65536 1 X X
loop(x,1000)
0 65536 0 X X
1 65536 0 X X
end loop
0 0 0 256 0
1 0 0 256 0
*/
