// Digital circuit 03.dig as structural Verilog
module _03 (
  input  [31:0] A,
  input  \input ,
  input  clk,
  input  reset,
  output [31:0] mean,
  output busy
);

  wire delay_1_out, not_1_out, not_2_out, Qa_t;
  wire [31:0] add_1_s, counter_1_out, div_1_q, multiplexer_1_out, sum;

  D_FF d_ff_1 (.D(\input ), .C(clk), .Q(busy), .nQ(Qa_t));
  Add #(.Bits(32)) add_1 (.a(A), .b(sum), .c_i(1'b0), .s(add_1_s));  // open: c_o
  not not_1 (not_1_out, clk);
  Multiplexer #(.Bits(32)) multiplexer_1 (.sel(busy), .in_0(sum), .in_1(add_1_s), .out(multiplexer_1_out));
  Delay #(.delayTime(10)) delay_1 (.in(busy), .out(delay_1_out));
  Counter #(.Bits(32)) counter_1 (.en(busy), .C(not_1_out), .clr(reset), .out(counter_1_out));  // open: ovf
  Register #(.Bits(32)) Load_Sum (.D(multiplexer_1_out), .C(clk), .en(delay_1_out), .Q(sum));
  Div #(.Bits(32)) div_1 (.a(sum), .b(counter_1_out), .q(div_1_q));  // open: r
  D_FF #(.Bits(32)) d_ff_2 (.D(div_1_q), .C(not_2_out), .Q(mean));  // open: nQ
  not not_2 (not_2_out, clk);

  // Other names for the same wires on the sheet: Qa = busy
endmodule

/* Test case Case1:
clk A input reset mean busy
0 0 0 0 0 0
1 0 0 0 0 0
0 0 0 1 0 0
1 0 0 1 0 0
0 0 0 0 0 0
1 0 0 0 0 0
0 5 1 0 X X
1 5 1 0 X X
0 5 0 0 X X
1 5 0 0 X X
loop(x,500)
end loop
0 0 0 0 5 0
1 0 0 0 5 0
*/

/* Test case Case2:
clk A input reset mean busy
0 0 0 0 0 0
1 0 0 0 0 0
0 0 0 1 0 0
1 0 0 1 0 0
0 0 0 0 0 0
1 0 0 0 0 0
0 5 1 0 X X
1 5 1 0 X X
0 5 0 0 X X
1 5 0 0 X X
loop(x,500)
end loop
0 0 0 0 5 0
1 0 0 0 5 0
0 15 1 0 X X
1 15 1 0 X X
0 15 0 0 X X
1 15 0 0 X X
loop(x,500)
end loop
0 0 0 0 10 0
1 0 0 0 10 0
*/

/* Test case Case3:
clk A input reset mean busy
0 0 0 0 0 0
1 0 0 0 0 0
0 0 0 1 0 0
1 0 0 1 0 0
0 0 0 0 0 0
1 0 0 0 0 0
0 65535 1 0 X X
1 65535 1 0 X X
0 65535 0 0 X X
1 65535 0 0 X X
loop(x,500)
end loop
0 0 0 0 65535 0
1 0 0 0 65535 0
0 65535 1 0 X X
1 65535 1 0 X X
0 65535 0 0 X X
1 65535 0 0 X X
loop(x,500)
end loop
0 0 0 0 65535 0
1 0 0 0 65535 0
*/

/* Test case Case4:
clk A input reset mean busy
0 0 0 0 0 0
1 0 0 0 0 0
0 0 0 1 0 0
1 0 0 1 0 0
0 0 0 0 0 0
1 0 0 0 0 0
0 1 1 0 X X
1 1 1 0 X X
0 1 0 0 X X
1 1 0 0 X X
loop(x,500)
end loop
0 0 0 0 1 0
1 0 0 0 1 0
0 2 1 0 X X
1 2 1 0 X X
0 2 0 0 X X
1 2 0 0 X X
loop(x,500)
end loop
0 0 0 0 1 0
1 0 0 0 1 0
0 3 1 0 X X
1 3 1 0 X X
0 3 0 0 X X
1 3 0 0 X X
loop(x,500)
end loop
0 0 0 0 2 0
1 0 0 0 2 0
0 4 1 0 X X
1 4 1 0 X X
0 4 0 0 X X
1 4 0 0 X X
loop(x,500)
end loop
0 0 0 0 2 0
1 0 0 0 2 0
0 5 1 0 X X
1 5 1 0 X X
0 5 0 0 X X
1 5 0 0 X X
loop(x,500)
end loop
0 0 0 0 3 0
1 0 0 0 3 0
0 6 1 0 X X
1 6 1 0 X X
0 6 0 0 X X
1 6 0 0 X X
loop(x,500)
end loop
0 0 0 0 3 0
1 0 0 0 3 0
0 7 1 0 X X
1 7 1 0 X X
0 7 0 0 X X
1 7 0 0 X X
loop(x,500)
end loop
0 0 0 0 4 0
1 0 0 0 4 0
0 8 1 0 X X
1 8 1 0 X X
0 8 0 0 X X
1 8 0 0 X X
loop(x,500)
end loop
0 0 0 0 4 0
1 0 0 0 4 0
0 9 1 0 X X
1 9 1 0 X X
0 9 0 0 X X
1 9 0 0 X X
loop(x,500)
end loop
0 0 0 0 5 0
1 0 0 0 5 0
0 10 1 0 X X
1 10 1 0 X X
0 10 0 0 X X
1 10 0 0 X X
loop(x,500)
end loop
0 0 0 0 5 0
1 0 0 0 5 0
0 11 1 0 X X
1 11 1 0 X X
0 11 0 0 X X
1 11 0 0 X X
loop(x,500)
end loop
0 0 0 0 6 0
1 0 0 0 6 0
0 12 1 0 X X
1 12 1 0 X X
0 12 0 0 X X
1 12 0 0 X X
loop(x,500)
end loop
0 0 0 0 6 0
1 0 0 0 6 0
0 13 1 0 X X
1 13 1 0 X X
0 13 0 0 X X
1 13 0 0 X X
loop(x,500)
end loop
0 0 0 0 7 0
1 0 0 0 7 0
0 14 1 0 X X
1 14 1 0 X X
0 14 0 0 X X
1 14 0 0 X X
loop(x,500)
end loop
0 0 0 0 7 0
1 0 0 0 7 0
0 15 1 0 X X
1 15 1 0 X X
0 15 0 0 X X
1 15 0 0 X X
loop(x,500)
end loop
0 0 0 0 8 0
1 0 0 0 8 0
*/

/* Test case Case5:
clk A input reset mean busy
0 0 0 0 0 0
1 0 0 0 0 0
0 0 0 1 0 0
1 0 0 1 0 0
0 0 0 0 0 0
1 0 0 0 0 0
0 0 1 0 X X
1 0 1 0 X X
0 0 0 0 X X
1 0 0 0 X X
loop(x,500)
end loop
0 0 0 0 0 0
1 0 0 0 0 0
0 0 1 0 X X
1 0 1 0 X X
0 0 0 0 X X
1 0 0 0 X X
loop(x,500)
end loop
0 0 0 0 0 0
1 0 0 0 0 0
0 0 1 0 X X
1 0 1 0 X X
0 0 0 0 X X
1 0 0 0 X X
loop(x,500)
end loop
0 0 0 0 0 0
1 0 0 0 0 0
0 0 1 0 X X
1 0 1 0 X X
0 0 0 0 X X
1 0 0 0 X X
loop(x,500)
end loop
0 0 0 0 0 0
1 0 0 0 0 0
0 0 1 0 X X
1 0 1 0 X X
0 0 0 0 X X
1 0 0 0 X X
loop(x,500)
end loop
0 0 0 0 0 0
1 0 0 0 0 0
0 0 1 0 X X
1 0 1 0 X X
0 0 0 0 X X
1 0 0 0 X X
loop(x,500)
end loop
0 0 0 0 0 0
1 0 0 0 0 0
0 0 1 0 X X
1 0 1 0 X X
0 0 0 0 X X
1 0 0 0 X X
loop(x,500)
end loop
0 0 0 0 0 0
1 0 0 0 0 0
0 0 1 0 X X
1 0 1 0 X X
0 0 0 0 X X
1 0 0 0 X X
loop(x,500)
end loop
0 0 0 0 0 0
1 0 0 0 0 0
0 0 1 0 X X
1 0 1 0 X X
0 0 0 0 X X
1 0 0 0 X X
loop(x,500)
end loop
0 0 0 0 0 0
1 0 0 0 0 0
0 0 1 0 X X
1 0 1 0 X X
0 0 0 0 X X
1 0 0 0 X X
loop(x,500)
end loop
0 0 0 0 0 0
1 0 0 0 0 0
*/
