// Digital circuit DigLo67_Project_Final.dig as structural Verilog
module DigLo67_Project_Final (
  input  [12:0] progIN,
  input  [7:0] M,
  input  [7:0] N,
  input  reset,
  input  progLoad,
  input  start,
  input  result,
  input  clk,
  output valid,
  output done,
  output [7:0] \output ,
  output greater_flag,
  output lesser_flag,
  output equal_flag,
  output [7:0] accA,
  output [7:0] accB,
  output [7:0] out_17,
  output [7:0] regC
);

  wire _0, _1, _2, _3, _4, _6, _7, _00101, _00111, _01000, _01010, _01011, _01100, _01101, _01110, _01111,
       _10000, _10110, _10111, _10111_eq, _10111_gr, _10111_le, _11101, _11110, _11110_hold, _11111,
       c1__gt__15, c2__gt__15, H0, H1, H2, H3, Hold1, isHalt_t, isPrime, Jump_eqorgr, Jump_equal,
       Jump_greater, Jump_lesser, loadddd, multiplexer_2_out, multiplexer_4_out, multiplexer_6_out,
       multiplexer_8_out, multiplexer_9_out, multiplexer_12_out, multiplexer_14_out, multiplexer_15_out,
       multiplexer_16_out, multiplexer_19_out, multiplexer_20_out, multiplexer_21_out, multiplexer_22_out,
       multiplexer_23_out, multiplexer_25_out, not_1_out, not_2_out, not_3_out, not_4_out, or_1_out,
       or_2_out, or_3_out, or_4_out, or_5_out, or_6_out, or_8_out, or_10_out, or_13_out, or_15_out,
       or_16_out, or_17_out, or_18_out, or_19_out, Qa;
  wire [0:0] Hold1_plus_2;
  wire [1:0] or_9_out, or_11_out, Qa_plus_b_plus_c, rom_1_d;
  wire [3:0] Ad_reset, add_1_s, counter_2_out, counter_3_out, rRAM_A2;
  wire [4:0] Operate;
  wire [7:0] _10001, _10010, _10011, _10100, _10101, _11000, _11001, _11010, _11011, _11100, div_2_r,
       Exponent, least, M_rRAM, most, multiplexer_1_out, multiplexer_3_out, multiplexer_11_out,
       multiplexer_13_out, multiplexer_17_out, multiplexer_18_out, N_rRAM, Operand, pRAM_adr, rRAM_A1,
       rRAM_Din;
  wire [12:8] pRAM_d2;
  wire [15:0] LCM_d;

  or or_1 (or_1_out, _01100, Jump_equal, Jump_eqorgr, Jump_lesser, Jump_greater);
  Counter #(.Bits(4)) counter_1 (.en(_6), .C(clk), .clr(~_6), .out(Ad_reset), .ovf(c2__gt__15));
  Counter #(.Bits(4)) counter_2 (.en(H2), .C(clk), .clr(~_11110_hold), .out(counter_2_out));  // open: ovf
  or or_2 (or_2_out, reset, result);
  Multiplexer #(.Selector_Bits(5), .Bits(8)) multiplexer_1 (
    .sel(Operate), .in_0(accA), .in_1(Operand), .in_2(accA), .in_3(accB), .in_4(accA), .in_5(accA),
    .in_6(regC), .in_7(accA), .in_8(accA), .in_9(pRAM_adr), .in_10(M_rRAM), .in_11(accA), .in_12(accA),
    .in_13(accA), .in_14(accA), .in_15(accA), .in_16(accA), .in_17(_10001), .in_18(_10010), .in_19(_10011),
    .in_20(_10100), .in_21(_10101), .in_22(Exponent), .in_23(accA), .in_24(_11000), .in_25(_11001),
    .in_26(_11010), .in_27(_11011), .in_28(_11100), .in_29(accA), .in_30(accA), .in_31(accA),
    .out(multiplexer_1_out));
  Multiplexer multiplexer_2 (.sel(or_2_out), .in_0(1'b0), .in_1(1'b1), .out(multiplexer_2_out));
  or or_3 (or_3_out, start, progLoad);
  Counter #(.Bits(4)) counter_3 (.en(_4), .C(clk), .clr(~_4), .out(counter_3_out), .ovf(c1__gt__15));
  Add #(.Bits(4)) add_1 (.a(counter_2_out), .b(4'b1110), .c_i(1'b0), .s(add_1_s));  // open: c_o
  Multiplexer #(.Bits(8)) multiplexer_3 (.sel(_0), .in_0(multiplexer_1_out), .in_1({8{1'b0}}), .out(multiplexer_3_out));
  Multiplexer multiplexer_4 (.sel(or_3_out), .in_0(1'b1), .in_1(1'b0), .out(multiplexer_4_out));
  or or_4 (or_4_out, _1, _2);
  Register #(.Bits(8)) u_accA (.D(multiplexer_3_out), .C(~clk), .en(or_5_out), .Q(accA));
  or or_5 (or_5_out, _0, start, _2);
  not not_1 (not_1_out, c2__gt__15);
  not not_2 (not_2_out, clk);
  or or_6 (or_6_out, _0, start);
  Multiplexer #(.Bits(4)) multiplexer_5 (.sel(_11110), .in_0(counter_3_out), .in_1(Operand[3:0]), .out(rRAM_A2));
  Seven_Seg_Hex seven_seg_hex_1 (.d(accA[7:4]), .dp(1'b0));
  Multiplexer #(.Selector_Bits(3)) multiplexer_6 (
    .sel({Qa, Qa_plus_b_plus_c}), .in_0(reset), .in_1(1'b0), .in_2(reset), .in_3(multiplexer_2_out),
    .in_4(1'b1), .in_5(multiplexer_4_out), .in_6(not_1_out), .in_7(1'b0), .out(multiplexer_6_out));
  CounterPreset #(.Bits(8)) Address (
    .en(or_4_out), .C(not_2_out), .dir(1'b0), .in(Operand), .ld(or_1_out), .clr(or_6_out), .out(out_17));  // open: ovf
  Seven_Seg_Hex seven_seg_hex_2 (.d(accA[3:0]), .dp(1'b0));
  D_FF d_ff_1 (.D(multiplexer_6_out), .C(clk), .Q(Qa));  // open: nQ
  Multiplexer #(.Selector_Bits(2), .Bits(8)) multiplexer_7 (
    .sel(or_9_out), .in_0(Operand), .in_1({4'b0000, Ad_reset}), .in_2({4'b0000, Operand[7:4]}),
    .in_3({4'b0000, add_1_s}), .out(rRAM_A1));
  or or_7 (or_9_out[0], H1, H2, _6);
  or or_8 (or_8_out, start, reset);
  or or_9 (or_9_out[1], H1, H2, _11110);
  Multiplexer multiplexer_8 (.sel(or_8_out), .in_0(1'b0), .in_1(1'b1), .out(multiplexer_8_out));
  or or_10 (or_10_out, reset, start);
  Multiplexer multiplexer_9 (.sel(result), .in_0(1'b1), .in_1(1'b0), .out(multiplexer_9_out));
  Multiplexer #(.Selector_Bits(2), .Bits(8)) multiplexer_10 (
    .sel(or_11_out), .in_0(accA), .in_1({8{1'b0}}), .in_2(most), .in_3(least), .out(rRAM_Din));
  or or_11 (or_11_out[0], H2, _6);
  Multiplexer #(.Selector_Bits(5), .Bits(8)) multiplexer_11 (
    .sel(Operate), .in_0(accB), .in_1(accB), .in_2(Operand), .in_3(accB), .in_4(accA), .in_5(accB),
    .in_6(accB), .in_7(accB), .in_8(accB), .in_9(accB), .in_10(accB), .in_11(accB), .in_12(accB),
    .in_13(accB), .in_14(accB), .in_15(accB), .in_16(accB), .in_17(accB), .in_18(accB), .in_19(accB),
    .in_20(accB), .in_21(accB), .in_22(accB), .in_23(accB), .in_24(accB), .in_25(accB), .in_26(accB),
    .in_27(accB), .in_28(accB), .in_29(accB), .in_30(accB), .in_31(accB), .out(multiplexer_11_out));
  Multiplexer #(.Selector_Bits(3)) multiplexer_12 (
    .sel({Qa, Qa_plus_b_plus_c}), .in_0(or_10_out), .in_1(start), .in_2(1'b1), .in_3(multiplexer_9_out),
    .in_4(1'b0), .in_5(multiplexer_8_out), .in_6(not_3_out), .in_7(1'b0), .out(multiplexer_12_out));
  not not_3 (not_3_out, c2__gt__15);
  RAMDualAccess #(.AddrBits(8), .Bits(13)) pRAM (
    .str(progLoad), .C(clk), .ld(1'b1), .A1(out_17), .Din1(progIN), .A2(Operand), .D1({Operate, Operand}),
    .D2({pRAM_d2, pRAM_adr}));
  or or_12 (or_11_out[1], H2, H1);
  Multiplexer #(.Bits(8)) multiplexer_13 (
    .sel(_0), .in_0(multiplexer_11_out), .in_1({8{1'b0}}), .out(multiplexer_13_out));
  D_FF d_ff_2 (.D(multiplexer_12_out), .C(clk), .Q(Qa_plus_b_plus_c[1]));  // open: nQ
  not not_4 (not_4_out, clk);
  Seven_Seg_Hex seven_seg_hex_3 (.d(accB[7:4]), .dp(1'b0));
  Register #(.Bits(8)) u_accB (.D(multiplexer_13_out), .C(~clk), .en(or_13_out), .Q(accB));
  or or_13 (or_13_out, _0, start, _2);
  or or_14 (loadddd, _6, _01011, H2, H1);
  RAMDualAccess #(.AddrBits(8), .Bits(8)) rRAM (
    .str(loadddd), .C(not_4_out), .ld(1'b1), .A1(rRAM_A1), .Din1(rRAM_Din), .A2({4'b0000, rRAM_A2}),
    .D1(M_rRAM), .D2(N_rRAM));
  Seven_Seg_Hex seven_seg_hex_4 (.d(accB[3:0]), .dp(1'b0));
  or or_15 (or_15_out, reset, result);
  or or_16 (or_16_out, start, result, reset);
  or or_17 (or_17_out, _11111, isHalt_t);
  Multiplexer multiplexer_14 (.sel(or_15_out), .in_0(1'b1), .in_1(1'b0), .out(multiplexer_14_out));
  Multiplexer multiplexer_15 (.sel(or_16_out), .in_0(1'b1), .in_1(1'b0), .out(multiplexer_15_out));
  or or_18 (or_18_out, greater_flag, equal_flag);
  ROM #(.AddrBits(5), .Bits(2)) rom_1 (.A(Operate), .sel(1'b1), .D(rom_1_d));
  Multiplexer #(.Selector_Bits(3)) multiplexer_16 (
    .sel({Qa, Qa_plus_b_plus_c}), .in_0(progLoad), .in_1(progLoad), .in_2(or_17_out),
    .in_3(multiplexer_14_out), .in_4(c1__gt__15), .in_5(multiplexer_15_out), .in_6(1'b0), .in_7(1'b0),
    .out(multiplexer_16_out));
  and and_1 (Jump_equal, _01101, equal_flag);
  and and_2 (Jump_greater, _01110, greater_flag);
  and and_3 (Jump_lesser, _01111, lesser_flag);
  and and_4 (Jump_eqorgr, _10000, or_18_out);
  Multiplexer #(.Selector_Bits(2), .Bits(8)) multiplexer_17 (
    .sel(rom_1_d), .in_0(regC), .in_1(accA), .in_2(M), .in_3(N), .out(multiplexer_17_out));
  Decoder #(.Selector_Bits(5)) decoder_1 (
    .sel(Operate), .out_5(_00101), .out_7(_00111), .out_8(_01000), .out_10(_01010), .out_11(_01011),
    .out_12(_01100), .out_13(_01101), .out_14(_01110), .out_15(_01111), .out_16(_10000), .out_22(_10110),
    .out_23(_10111), .out_29(_11101), .out_30(_11110), .out_31(_11111));  // open: out_0, out_1, out_2, out_3, out_4, out_6, out_9, out_17, out_18, out_19, out_20, out_21, out_24, out_25, out_26, out_27, out_28
  D_FF d_ff_3 (.D(_11111), .C(clk), .Q(isHalt_t));  // open: nQ
  D_FF d_ff_4 (.D(multiplexer_16_out), .C(clk), .Q(Qa_plus_b_plus_c[0]));  // open: nQ
  Multiplexer #(.Bits(8)) multiplexer_18 (
    .sel(reset), .in_0(multiplexer_17_out), .in_1({8{1'b0}}), .out(multiplexer_18_out));
  Register #(.Bits(8)) u_RegC (.D(multiplexer_18_out), .C(clk), .en(1'b1), .Q(regC));
  Decoder #(.Selector_Bits(3)) decoder_2 (
    .sel({Qa, Qa_plus_b_plus_c}), .out_0(_0), .out_1(_1), .out_2(_2), .out_3(_3), .out_4(_4), .out_5(done),
    .out_6(_6), .out_7(_7));
  Div #(.Bits(8)) div_1 (.a(accA), .b(accB), .q(_10100), .r(_10101));
  Div #(.Bits(8)) div_2 (.a(accB), .b(8'h8), .r(div_2_r));  // open: q
  Add #(.Bits(8)) add_2 (.a(accA), .b(accB), .c_i(1'b0), .s(_10001));  // open: c_o
  Sub #(.Bits(8)) sub_1 (.a(accA), .b(accB), .c_i(1'b0), .s(_10010));  // open: c_o
  Mul #(.Bits(4)) mul_1 (.a(accA[3:0]), .b(accB[3:0]), .mul(_10011));
  ROM #(.AddrBits(6), .Bits(8)) u_Exponent (.A({accA[2:0], accB[2:0]}), .sel(1'b1), .D(Exponent));
  Comparator #(.Bits(8)) comparator_1 (.a(accA), .b(accB), .gt(_10111_gr), .eq(_10111_eq), .lt(_10111_le));
  Multiplexer multiplexer_19 (.sel(_10111), .in_0(isPrime), .in_1(_10111_eq), .out(multiplexer_19_out));
  ROM #(.AddrBits(16), .Bits(16)) LCM (.A({M_rRAM, N_rRAM}), .sel(_11110), .D(LCM_d));
  BarrelShifter #(.Bits(8)) barrelshifter_1 (.in(accA), .shift(div_2_r[3:0]), .out(_11100));
  Multiplexer multiplexer_20 (.sel(reset), .in_0(multiplexer_19_out), .in_1(1'b0), .out(multiplexer_20_out));
  or or_19 (or_19_out, _10111, reset, _11101);
  Register u_equal_flag (.D(multiplexer_20_out), .C(clk), .en(or_19_out), .Q(equal_flag));
  D_FF #(.Bits(8)) d_ff_5 (.D(LCM_d[7:0]), .C(H1), .Q(least));  // open: nQ
  D_FF #(.Bits(8)) d_ff_6 (.D(LCM_d[15:8]), .C(H1), .Q(most));  // open: nQ
  assign _11000 = ~accA;  // Not not_5, 8 bits wide
  assign _11001 = accA & accB;  // And and_5, 8 bits wide
  assign _11010 = accA | accB;  // Or or_20, 8 bits wide
  assign _11011 = accA ^ accB;  // XOr xor_1, 8 bits wide
  ROM #(.AddrBits(8)) u_isPrime (.A(accA), .sel(1'b1), .D(isPrime));
  Multiplexer multiplexer_21 (.sel(reset), .in_0(_10111_gr), .in_1(1'b0), .out(multiplexer_21_out));
  Multiplexer multiplexer_22 (.sel(reset), .in_0(_10111_le), .in_1(1'b0), .out(multiplexer_22_out));
  Multiplexer #(.Selector_Bits(2)) multiplexer_23 (
    .sel({Hold1, Hold1_plus_2[0]}), .in_0(1'b0), .in_1(1'b1), .in_2(1'b1), .in_3(1'b0),
    .out(multiplexer_23_out));
  or or_21 (valid, _3, _4, done);
  D_FF d_ff_7 (.D(multiplexer_23_out), .C(~clk), .Q(Hold1));  // open: nQ
  Multiplexer #(.Bits(8)) multiplexer_24 (.sel(_4), .in_0({8{1'b0}}), .in_1(N_rRAM), .out(\output ));
  Register u_greater_flag (.D(multiplexer_21_out), .C(clk), .en(_10111), .Q(greater_flag));
  Register u_lesser_flag (.D(multiplexer_22_out), .C(clk), .en(_10111), .Q(lesser_flag));
  Multiplexer #(.Selector_Bits(2)) multiplexer_25 (
    .sel({Hold1, Hold1_plus_2[0]}), .in_0(_11110), .in_1(1'b0), .in_2(1'b1), .in_3(1'b0),
    .out(multiplexer_25_out));
  Seven_Seg_Hex seven_seg_hex_5 (.d(\output [7:4]), .dp(1'b0));
  D_FF d_ff_8 (.D(multiplexer_25_out), .C(~clk), .Q(Hold1_plus_2[0]));  // open: nQ
  or or_22 (_11110_hold, H3, H2, H1);
  Seven_Seg_Hex seven_seg_hex_6 (.d(\output [3:0]), .dp(1'b0));
  Decoder #(.Selector_Bits(2)) decoder_3 (
    .sel({Hold1, Hold1_plus_2[0]}), .out_0(H0), .out_1(H1), .out_2(H2), .out_3(H3));

  // Other names for the same wires on the sheet: Operand_least[3:0] = Operand[3:0]; Operand_most[3:0] = Operand[7:4];
  //   _5 = done; Address[7:0] = out_17; Hold1_plus_2[1] = Hold1; Hold2 = Hold1_plus_2[0]; isHalt = _11111;
  //   Jump_nocon = _01100; output_t[7:0] = N_rRAM; Prog_In[12:0] = progIN; Prog_Load = progLoad;
  //   Qa_plus_b_plus_c[2] = Qa; Qb = Qa_plus_b_plus_c[1]; Qc = Qa_plus_b_plus_c[0]; reset_in = reset;
  //   result_in = result; rRAM_adr[7:0] = M_rRAM; start_in = start

  // Notes on the sheet:
  //   Member
  //   1. Phathanan Jareonphon 6733169821 - Main
  //   2. Sippawit Chamchomdao 6733272721 - Main
  //   3. Thanasorn Nonmuang 6733098921
  //   Testcase
  //   Input
  //   Address
  //   rRAM
  //   accA
  //   Control Unit
  //   pRAM
  //   accB
  //   Jump+Check
  //   regC
  //   DEMUX
  //   contents of rom_1 (hex, n*v repeats v):
  //   5*0,1,0,2,3
  //   Adder
  //   Substract
  //   Multiple
  //   Division / Modulo
  //   Shift Left
  //   Exponent
  //   Flag
  //   LCM
  //   Comparation
  //   contents of Exponent (hex, n*v repeats v):
  //   1,7*0,9*1,2,4,8,10,20,40,80,1,3,9,1b,51,f3,2d9,88b,1,4,10,40,256
  //   ,1024,4096,16843,1,5,19,7d,271,c35,3d09,1312d,1,6,24,d8,510,1e60
  //   ,b640,44580,1,7,31,157,961,41a7,1cb91,c90f7
  //   contents of LCM (hex, n*v repeats v):
  //   257*0,1,2,3,4,5,6,7,8,9,a,b,c,d,e,f,10,11,12,13,14,15,16,17,18
  //   ,19,1a,1b,1c,1d,1e,1f,20,21,22,23,24,25,26,27,28,29,2a,2b,2c,2d
  //   ,2e,2f,30,31,32,33,34,35,36,37,38,39,3a,3b,3c,3d,3e,3f,40,41,42
  //   ,43,44,45,46,47,48,49,4a,4b,4c,4d,4e,4f,50,51,52,53,54,55,56,57
  //   ,58,59,5a,5b,5c,5d,5e,5f,60,61,62,63,64,65,66,67,68,69,6a,6b,6c
  //   ,6d,6e,6f,70,71,72,73,74,75,76,77,78,79,7a,7b,7c,7d,7e,7f,80,81
  //   ,82,83,84,85,86,87,88,89,8a,8b,8c,8d,8e,8f,90,91,92,93,94,95,96
  //   ,97,98,99,9a,9b,9c,9d,9e,9f,a0,a1,a2,a3,a4,a5,a6,a7,a8,a9,aa,ab
  //   ,ac,ad,ae,af,b0,b1,b2,b3,b4,b5,b6,b7,b8,b9,ba,bb,bc,bd,be,bf,c0
  //   ,c1,c2,c3,c4,c5,c6,c7,c8,c9,ca,cb,cc,cd,ce,cf,d0,d1,d2,d3,d4,d5
  //   ,d6,d7,d8,d9,da,db,dc,dd,de,df,e0,e1,e2,e3,e4,e5,e6,e7,e8,e9,ea
  //   ,eb,ec,ed,ee,ef,f0,f1,f2,f3,f4,f5,f6,f7,f8,f9,fa,fb,fc,fd,fe,ff
  //   ,0,2,2,6,4,a,6,e,8,12,a,16,c,1a,e,1e,10,22,12,26,14,2a,16,2e,18
  //   ,32,1a,36,1c,3a,1e,3e,20,42,22,46,24,4a,26,4e,28,52,2a,56,2c,5a
  //   ,2e,5e,30,62,32,66,34,6a,36,6e,38,72,3a,76,3c,7a,3e,7e,40,82,42
  //   ,86,44,8a,46,8e,48,92,4a,96,4c,9a,4e,9e,50,a2,52,a6,54,aa,56,ae
  //   ,58,b2,5a,b6,5c,ba,5e,be,60,c2,62,c6,64,ca,66,ce,68,d2,6a,d6,6c
  //   ,da,6e,de,70,e2,72,e6,74,ea,76,ee,78,f2,7a,f6,7c,fa,7e,fe,80,102
  //   ,82,106,84,10a,86,10e,88,112,8a,116,8c,11a,8e,11e,90,122,92,126
  //   ,94,12a,96,12e,98,132,9a,136,9c,13a,9e,13e,a0,142,a2,146,a4,14a
  //   ,a6,14e,a8,152,aa,156,ac,15a,ae,15e,b0,162,b2,166,b4,16a,b6,16e
  //   ,b8,172,ba,176,bc,17a,be,17e,c0,182,c2,186,c4,18a,c6,18e,c8,192
  //   ,ca,196,cc,19a,ce,19e,d0,1a2,d2,1a6,d4,1aa,d6,1ae,d8,1b2,da,1b6
  //   ,dc,1ba,de,1be,e0,1c2,e2,1c6,e4,1ca,e6,1ce,e8,1d2,ea,1d6,ec,1da
  //   ,ee,1de,f0,1e2,f2,1e6,f4,1ea,f6,1ee,f8,1f2,fa,1f6,fc,1fa,fe,1fe
  //   ,0,3,6,3,c,f,6,15,18,9,1e,21,c,27,2a,f,30,33,12,39,3c,15,42,45
  //   ,18,4b,4e,1b,54,57,1e,5d,60,21,66,69,24,6f,72,27,78,7b,2a,81,84
  //   ,2d,8a,8d,30,93,96,33,9c,9f,36,a5,a8,39,ae,b1,3c,b7,ba,3f,c0,c3
  //   ,42,c9,cc,45,d2,d5,48,db,de,4b,e4,e7,4e,ed,f0,51,f6,f9,54,ff,102
  //   ,57,108,10b,5a,111,114,5d,11a,11d,60,123,126,63,12c,12f,66,135
  //   ,138,69,13e,141,6c,147,14a,6f,150,153,72,159,15c,75,162,165,78
  //   ,16b,16e,7b,174,177,7e,17d,180,81,186,189,84,18f,192,87,198,19b
  //   ,8a,1a1,1a4,8d,1aa,1ad,90,1b3,1b6,93,1bc,1bf,96,1c5,1c8,99,1ce
  //   ,1d1,9c,1d7,1da,9f,1e0,1e3,a2,1e9,1ec,a5,1f2,1f5,a8,1fb,1fe,ab
  //   ,204,207,ae,20d,210,b1,216,219,b4,21f,222,b7,228,22b,ba,231,234
  //   ,bd,23a,23d,c0,243,246,c3,24c,24f,c6,255,258,c9,25e,261,cc,267
  //   ,26a,cf,270,273,d2,279,27c,d5,282,285,d8,28b,28e,db,294,297,de
  //   ,29d,2a0,e1,2a6,2a9,e4,2af,2b2,e7,2b8,2bb,ea,2c1,2c4,ed,2ca,2cd
  //   ,f0,2d3,2d6,f3,2dc,2df,f6,2e5,2e8,f9,2ee,2f1,fc,2f7,2fa,ff,0,4,4
  //   ,c,4,14,c,1c,8,24,14,2c,c,34,1c,3c,10,44,24,4c,14,54,2c,5c,18
  //   ,64,34,6c,1c,74,3c,7c,20,84,44,8c,24,94,4c,9c,28,a4,54,ac,2c,b4
  //   ,5c,bc,30,c4,64,cc,34,d4,6c,dc,38,e4,74,ec,3c,f4,7c,fc,40,104
  //   ,84,10c,44,114,8c,11c,48,124,94,12c,4c,134,9c,13c,50,144,a4,14c
  //   ,54,154,ac,15c,58,164,b4,16c,5c,174,bc,17c,60,184,c4,18c,64,194
  //   ,cc,19c,68,1a4,d4,1ac,6c,1b4,dc,1bc,70,1c4,e4,1cc,74,1d4,ec,1dc
  //   ,78,1e4,f4,1ec,7c,1f4,fc,1fc,80,204,104,20c,84,214,10c,21c,88
  //   ,224,114,22c,8c,234,11c,23c,90,244,124,24c,94,254,12c,25c,98,264
  //   ,134,26c,9c,274,13c,27c,a0,284,144,28c,a4,294,14c,29c,a8,2a4,154
  //   ,2ac,ac,2b4,15c,2bc,b0,2c4,164,2cc,b4,2d4,16c,2dc,b8,2e4,174,2ec
  //   ,bc,2f4,17c,2fc,c0,304,184,30c,c4,314,18c,31c,c8,324,194,32c,cc
  //   ,334,19c,33c,d0,344,1a4,34c,d4,354,1ac,35c,d8,364,1b4,36c,dc,374
  //   ,1bc,37c,e0,384,1c4,38c,e4,394,1cc,39c,e8,3a4,1d4,3ac,ec,3b4,1dc
  //   ,3bc,f0,3c4,1e4,3cc,f4,3d4,1ec,3dc,f8,3e4,1f4,3ec,fc,3f4,1fc,3fc
  //   ,0,5,a,f,14,5,1e,23,28,2d,a,37,3c,41,46,f,50,55,5a,5f,14,69,6e
  //   ,73,78,19,82,87,8c,91,1e,9b,a0,a5,aa,23,b4,b9,be,c3,28,cd,d2,d7
  //   ,dc,2d,e6,eb,f0,f5,32,ff,104,109,10e,37,118,11d,122,127,3c,131
  //   ,136,13b,140,41,14a,14f,154,159,46,163,168,16d,172,4b,17c,181
  //   ,186,18b,50,195,19a,19f,1a4,55,1ae,1b3,1b8,1bd,5a,1c7,1cc,1d1
  //   ,1d6,5f,1e0,1e5,1ea,1ef,64,1f9,1fe,203,208,69,212,217,21c,221
  //   ,6e,22b,230,235,23a,73,244,249,24e,253,78,25d,262,267,26c,7d,276
  //   ,27b,280,285,82,28f,294,299,29e,87,2a8,2ad,2b2,2b7,8c,2c1,2c6
  //   ,2cb,2d0,91,2da,2df,2e4,2e9,96,2f3,2f8,2fd,302,9b,30c,311,316
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  //   Not
  //   And
  //   Or
  //   XOR
  //   isPrime
  //   contents of isPrime (hex, n*v repeats v):
  //   0,0,1,1,0,1,0,1,0,0,0,1,0,1,0,0,0,1,0,1,0,0,0,1,5*0,1,0,1,5*0
  //   ,1,0,0,0,1,0,1,0,0,0,1,5*0,1,5*0,1,0,1,5*0,1,0,0,0,1,0,1,5*0,1
  //   ,0,0,0,1,5*0,1,7*0,1,0,0,0,1,0,1,0,0,0,1,0,1,0,0,0,1,13*0,1,0,0,0
  //   ,1,5*0,1,0,1,9*0,1,0,1,5*0,1,5*0,1,0,0,0,1,5*0,1,5*0,1,0,1,9*0
  //   ,1,0,1,0,0,0,1,0,1,11*0,1,11*0,1,0,0,0,1,0,1,0,0,0,1,5*0,1,0,1
  //   ,9*0,1
  //   Output
  //   LCM - Control
endmodule

/* Test case 01_P01T01:
M N progIN reset progLoad start result clk valid done output
0 0 0 0 0 0 0 0 x x x
0 0 0 0 0 0 0 1 x x x
0 0 0 1 0 0 0 0 x x x
0 0 0 1 0 0 0 1 0 0 0
0 0 0 0 0 0 0 0 0 0 0
0 0 0 0 0 0 0 1 0 0 0
0 0 0 0 0 0 0 0 0 0 0
0 0 0 0 0 0 0 1 0 0 0
0 0 0 0 0 0 0 0 0 0 0
0 0 0 0 0 0 0 1 0 0 0
0 0 0 0 0 0 0 0 0 0 0
0 0 0 0 0 0 0 1 0 0 0
0 0 0 0 0 0 0 0 0 0 0
0 0 0 0 0 0 0 1 0 0 0
0 0 0 0 0 0 0 0 0 0 0
0 0 0 0 0 0 0 1 0 0 0
0 0 0 0 0 0 0 0 0 0 0
0 0 0 0 0 0 0 1 0 0 0
0 0 0 0 0 0 0 0 0 0 0
0 0 0 0 0 0 0 1 0 0 0
0 0 0 0 0 0 0 0 0 0 0
0 0 0 0 0 0 0 1 0 0 0
0 0 0 0 0 0 0 0 0 0 0
0 0 0 0 0 0 0 1 0 0 0
0 0 0 0 0 0 0 0 0 0 0
0 0 0 0 0 0 0 1 0 0 0
0 0 0 0 0 0 0 0 0 0 0
0 0 0 0 0 0 0 1 0 0 0
0 0 0 0 0 0 0 0 0 0 0
0 0 0 0 0 0 0 1 0 0 0
0 0 0 0 0 0 0 0 0 0 0
0 0 0 0 0 0 0 1 0 0 0
0 0 0 0 0 0 0 0 0 0 0
0 0 0 0 0 0 0 1 0 0 0
0 0 0 0 0 0 0 0 0 0 0
0 0 0 0 0 0 0 1 0 0 0
0 0 0 0 0 0 0 0 0 0 0
0 0 0 0 0 0 0 1 0 0 0
0 0 0 0 0 0 0 0 0 0 0
0 0 0 0 0 0 0 1 0 0 0
0 0 0 0 0 0 0 0 0 0 0
0 0 0 0 0 0 0 1 0 0 0
0 0 271 0 1 0 0 0 0 0 0
0 0 271 0 1 0 0 1 0 0 0
0 0 565 0 1 0 0 0 0 0 0
0 0 565 0 1 0 0 1 0 0 0
0 0 4352 0 1 0 0 0 0 0 0
0 0 4352 0 1 0 0 1 0 0 0
0 0 2819 0 1 0 0 0 0 0 0
0 0 2819 0 1 0 0 1 0 0 0
0 0 7936 0 1 0 0 0 0 0 0
0 0 7936 0 1 0 0 1 0 0 0
0 0 0 0 0 1 0 0 0 0 0
0 0 0 0 0 1 0 1 0 0 0
0 0 0 0 0 0 0 0 x 0 0
0 0 0 0 0 0 0 1 x 0 0
0 0 0 0 0 0 0 0 x 0 0
0 0 0 0 0 0 0 1 x 0 0
0 0 0 0 0 0 0 0 x 0 0
0 0 0 0 0 0 0 1 x 0 0
0 0 0 0 0 0 0 0 x 0 0
0 0 0 0 0 0 0 1 x 0 0
0 0 0 0 0 0 0 0 x 0 0
0 0 0 0 0 0 0 1 x 0 0
0 0 0 0 0 0 0 0 x 0 0
0 0 0 0 0 0 0 1 x 0 0
0 0 0 0 0 0 0 0 x 0 0
0 0 0 0 0 0 0 1 x 0 0
0 0 0 0 0 0 0 0 x 0 0
0 0 0 0 0 0 0 1 x 0 0
0 0 0 0 0 0 0 0 x 0 0
0 0 0 0 0 0 0 1 x 0 0
0 0 0 0 0 0 0 0 x 0 0
0 0 0 0 0 0 0 1 x 0 0
0 0 0 0 0 0 0 0 x 0 0
0 0 0 0 0 0 0 1 x 0 0
0 0 0 0 0 0 0 0 x 0 0
0 0 0 0 0 0 0 1 x 0 0
0 0 0 0 0 0 0 0 x 0 0
0 0 0 0 0 0 0 1 x 0 0
0 0 0 0 0 0 0 0 x 0 0
0 0 0 0 0 0 0 1 x 0 0
0 0 0 0 0 0 0 0 x 0 0
0 0 0 0 0 0 0 1 x 0 0
0 0 0 0 0 0 0 0 x 0 0
0 0 0 0 0 0 0 1 x 0 0
0 0 0 0 0 0 0 0 x 0 0
0 0 0 0 0 0 0 1 x 0 0
0 0 0 0 0 0 0 0 x 0 0
0 0 0 0 0 0 0 1 x 0 0
0 0 0 0 0 0 0 0 x 0 0
0 0 0 0 0 0 0 1 x 0 0
0 0 0 0 0 0 0 0 x 0 0
0 0 0 0 0 0 0 1 x 0 0
0 0 0 0 0 0 0 0 x 0 0
0 0 0 0 0 0 0 1 x 0 0
0 0 0 0 0 0 0 0 x 0 0
0 0 0 0 0 0 0 1 x 0 0
0 0 0 0 0 0 0 0 x 0 0
0 0 0 0 0 0 0 1 x 0 0
0 0 0 0 0 0 0 0 x 0 0
0 0 0 0 0 0 0 1 x 0 0
0 0 0 0 0 0 0 0 x 0 0
0 0 0 0 0 0 0 1 x 0 0
0 0 0 0 0 0 0 0 x 0 0
0 0 0 0 0 0 0 1 1 0 0
0 0 0 0 0 0 1 0 1 0 0
0 0 0 0 0 0 1 1 1 0 0
0 0 0 0 0 0 0 0 1 0 0
0 0 0 0 0 0 0 1 1 0 0
0 0 0 0 0 0 0 0 1 0 0
0 0 0 0 0 0 0 1 1 0 0
0 0 0 0 0 0 0 0 1 0 0
0 0 0 0 0 0 0 1 1 0 68
0 0 0 0 0 0 0 0 1 0 68
0 0 0 0 0 0 0 1 1 0 0
0 0 0 0 0 0 0 0 1 0 0
0 0 0 0 0 0 0 1 1 0 0
0 0 0 0 0 0 0 0 1 0 0
0 0 0 0 0 0 0 1 1 0 0
0 0 0 0 0 0 0 0 1 0 0
0 0 0 0 0 0 0 1 1 0 0
0 0 0 0 0 0 0 0 1 0 0
0 0 0 0 0 0 0 1 1 0 0
0 0 0 0 0 0 0 0 1 0 0
0 0 0 0 0 0 0 1 1 0 0
0 0 0 0 0 0 0 0 1 0 0
0 0 0 0 0 0 0 1 1 0 0
0 0 0 0 0 0 0 0 1 0 0
0 0 0 0 0 0 0 1 1 0 0
0 0 0 0 0 0 0 0 1 0 0
0 0 0 0 0 0 0 1 1 0 0
0 0 0 0 0 0 0 0 1 0 0
0 0 0 0 0 0 0 1 1 0 0
0 0 0 0 0 0 0 0 1 0 0
0 0 0 0 0 0 0 1 1 0 0
0 0 0 0 0 0 0 0 1 0 0
0 0 0 0 0 0 0 1 1 0 0
0 0 0 0 0 0 0 0 1 0 0
0 0 0 0 0 0 0 1 1 1 0
0 0 0 0 0 0 0 0 1 1 0
0 0 0 0 0 0 0 1 1 1 0
0 0 0 0 0 0 0 0 1 1 0
*/

/* Test case 07_mistake:
M	N	progIN	reset	progLoad	start	result	clk	valid	done	output
0	0	0	0	0	0	0	0	x	x	x
0	0	0	0	0	0	0	1	x	x	x
0	0	0	1	0	0	0	0	x	x	x
0	0	0	1	0	0	0	1	0	0	x
0	0	0	0	0	0	0	0	0	0	x
0	0	0	0	0	0	0	1	0	0	x
0	0	0	0	0	0	0	0	0	0	x
0	0	0	0	0	0	0	1	0	0	x
0	0	0	0	0	0	0	0	0	0	x
0	0	0	0	0	0	0	1	0	0	x
0	0	0	0	0	0	0	0	0	0	x
0	0	0	0	0	0	0	1	0	0	x
0	0	0	0	0	0	0	0	0	0	x
0	0	0	0	0	0	0	1	0	0	x
0	0	0	0	0	0	0	0	0	0	x
0	0	0	0	0	0	0	1	0	0	x
0	0	0	0	0	0	0	0	0	0	x
0	0	0	0	0	0	0	1	0	0	x
0	0	0	0	0	0	0	0	0	0	x
0	0	0	0	0	0	0	1	0	0	x
0	0	0	0	0	0	0	0	0	0	x
0	0	0	0	0	0	0	1	0	0	x
0	0	0	0	0	0	0	0	0	0	x
0	0	0	0	0	0	0	1	0	0	x
0	0	0	0	0	0	0	0	0	0	x
0	0	0	0	0	0	0	1	0	0	x
0	0	0	0	0	0	0	0	0	0	x
0	0	0	0	0	0	0	1	0	0	x
0	0	0	0	0	0	0	0	0	0	x
0	0	0	0	0	0	0	1	0	0	x
0	0	0	0	0	0	0	0	0	0	x
0	0	0	0	0	0	0	1	0	0	x
0	0	0	0	0	0	0	0	0	0	x
0	0	0	0	0	0	0	1	0	0	x
0	0	0	0	0	0	0	0	0	0	x
0	0	0	0	0	0	0	1	0	0	x
0	0	0	0	0	0	0	0	0	0	x
0	0	0	0	0	0	0	1	0	0	x
0	0	0	0	0	0	0	0	0	0	x
0	0	0	0	0	0	0	1	0	0	x
0	0	0	0	0	0	0	0	0	0	x
0	0	0	0	0	0	0	1	0	0	x
0	0	1792	0	1	0	0	0	0	0	x
0	0	1792	0	1	0	0	1	0	0	x
0	0	1536	0	1	0	0	0	0	0	x
0	0	1536	0	1	0	0	1	0	0	x
0	0	2817	0	1	0	0	0	0	0	x
0	0	2817	0	1	0	0	1	0	0	x
0	0	2048	0	1	0	0	0	0	0	x
0	0	2048	0	1	0	0	1	0	0	x
0	0	1536	0	1	0	0	0	0	0	x
0	0	1536	0	1	0	0	1	0	0	x
0	0	2818	0	1	0	0	0	0	0	x
0	0	2818	0	1	0	0	1	0	0	x
0	0	1024	0	1	0	0	0	0	0	x
0	0	1024	0	1	0	0	1	0	0	x
0	0	2561	0	1	0	0	0	0	0	x
0	0	2561	0	1	0	0	1	0	0	x
0	0	4864	0	1	0	0	0	0	0	x
0	0	4864	0	1	0	0	1	0	0	x
0	0	2819	0	1	0	0	0	0	0	x
0	0	2819	0	1	0	0	1	0	0	x
0	0	2561	0	1	0	0	0	0	0	x
0	0	2561	0	1	0	0	1	0	0	x
0	0	5120	0	1	0	0	0	0	0	x
0	0	5120	0	1	0	0	1	0	0	x
0	0	2820	0	1	0	0	0	0	0	x
0	0	2820	0	1	0	0	1	0	0	x
0	0	7936	0	1	0	0	0	0	0	x
0	0	7936	0	1	0	0	1	0	0	x
15	7	0	0	0	1	0	0	0	0	x
15	7	0	0	0	1	0	1	0	0	x
15	7	0	0	0	0	0	0	x	0	x
15	7	0	0	0	0	0	1	x	0	x
15	7	0	0	0	0	0	0	x	0	x
15	7	0	0	0	0	0	1	x	0	x
15	7	0	0	0	0	0	0	x	0	x
15	7	0	0	0	0	0	1	x	0	x
15	7	0	0	0	0	0	0	x	0	x
15	7	0	0	0	0	0	1	x	0	x
15	7	0	0	0	0	0	0	x	0	x
15	7	0	0	0	0	0	1	x	0	x
15	7	0	0	0	0	0	0	x	0	x
15	7	0	0	0	0	0	1	x	0	x
15	7	0	0	0	0	0	0	x	0	x
15	7	0	0	0	0	0	1	x	0	x
15	7	0	0	0	0	0	0	x	0	x
15	7	0	0	0	0	0	1	x	0	x
15	7	0	0	0	0	0	0	x	0	x
15	7	0	0	0	0	0	1	x	0	x
15	7	0	0	0	0	0	0	x	0	x
15	7	0	0	0	0	0	1	x	0	x
15	7	0	0	0	0	0	0	x	0	x
15	7	0	0	0	0	0	1	x	0	x
15	7	0	0	0	0	0	0	x	0	x
15	7	0	0	0	0	0	1	x	0	x
15	7	0	0	0	0	0	0	x	0	x
15	7	0	0	0	0	0	1	x	0	x
15	7	0	0	0	0	0	0	x	0	x
15	7	0	0	0	0	0	1	x	0	x
15	7	0	0	0	0	0	0	x	0	x
15	7	0	0	0	0	0	1	x	0	x
15	7	0	0	0	0	0	0	x	0	x
15	7	0	0	0	0	0	1	x	0	x
15	7	0	0	0	0	0	0	x	0	x
15	7	0	0	0	0	0	1	x	0	x
15	7	0	0	0	0	0	0	x	0	x
15	7	0	0	0	0	0	1	x	0	x
15	7	0	0	0	0	0	0	x	0	x
15	7	0	0	0	0	0	1	x	0	x
15	7	0	0	0	0	0	0	x	0	x
0	0	0	0	0	0	0	1	x	0	x
0	0	0	0	0	0	0	0	x	0	x
0	0	0	0	0	0	0	1	x	0	x
0	0	0	0	0	0	0	0	x	0	x
0	0	0	0	0	0	0	1	x	0	x
0	0	0	0	0	0	0	0	x	0	x
0	0	0	0	0	0	0	1	x	0	x
0	0	0	0	0	0	0	0	x	0	x
0	0	0	0	0	0	0	1	x	0	x
0	0	0	0	0	0	0	0	x	0	x
0	0	0	0	0	0	0	1	x	0	x
0	0	0	0	0	0	0	0	x	0	x
0	0	0	0	0	0	0	1	x	0	x
0	0	0	0	0	0	0	0	x	0	x
0	0	0	0	0	0	0	1	x	0	x
0	0	0	0	0	0	0	0	x	0	x
0	0	0	0	0	0	0	1	x	0	x
0	0	0	0	0	0	0	0	x	0	x
0	0	0	0	0	0	0	1	x	0	x
0	0	0	0	0	0	0	0	x	0	x
0	0	0	0	0	0	0	1	x	0	x
0	0	0	0	0	0	0	0	x	0	x
0	0	0	0	0	0	0	1	x	0	x
0	0	0	0	0	0	0	0	x	0	x
0	0	0	0	0	0	0	1	x	0	x
0	0	0	0	0	0	0	0	x	0	x
0	0	0	0	0	0	0	1	x	0	x
0	0	0	0	0	0	0	0	x	0	x
0	0	0	0	0	0	0	1	x	0	x
0	0	0	0	0	0	0	0	x	0	x
0	0	0	0	0	0	0	1	x	0	x
0	0	0	0	0	0	0	0	x	0	x
0	0	0	0	0	0	0	1	x	0	x
0	0	0	0	0	0	0	0	x	0	x
0	0	0	0	0	0	0	1	x	0	x
0	0	0	0	0	0	0	0	x	0	x
0	0	0	0	0	0	0	1	x	0	x
0	0	0	0	0	0	0	0	x	0	x
0	0	0	0	0	0	0	1	x	0	x
0	0	0	0	0	0	0	0	x	0	x
0	0	0	0	0	0	0	1	x	0	x
0	0	0	0	0	0	0	0	x	0	x
0	0	0	0	0	0	0	1	x	0	x
0	0	0	0	0	0	0	0	x	0	x
0	0	0	0	0	0	0	1	x	0	x
0	0	0	0	0	0	0	0	x	0	x
0	0	0	0	0	0	0	1	x	0	x
0	0	0	0	0	0	0	0	x	0	x
0	0	0	0	0	0	0	1	x	0	x
0	0	0	0	0	0	0	0	x	0	x
0	0	0	0	0	0	0	1	x	0	x
0	0	0	0	0	0	0	0	x	0	x
0	0	0	0	0	0	0	1	x	0	x
0	0	0	0	0	0	0	0	x	0	x
0	0	0	0	0	0	0	1	x	0	x
0	0	0	0	0	0	0	0	x	0	x
0	0	0	0	0	0	0	1	x	0	x
0	0	0	0	0	0	0	0	x	0	x
0	0	0	0	0	0	0	1	x	0	x
0	0	0	0	0	0	0	0	x	0	x
0	0	0	0	0	0	0	1	x	0	x
0	0	0	0	0	0	0	0	x	0	x
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*/

/* Test case 08_mistake:
M	N	progIN	reset	progLoad	start	result	clk	valid	done	output
0	0	0	0	0	0	0	0	x	x	x
0	0	0	0	0	0	0	1	x	x	x
0	0	0	1	0	0	0	0	x	x	x
0	0	0	1	0	0	0	1	0	0	x
0	0	0	0	0	0	0	0	0	0	x
0	0	0	0	0	0	0	1	0	0	x
0	0	0	0	0	0	0	0	0	0	x
0	0	0	0	0	0	0	1	0	0	x
0	0	0	0	0	0	0	0	0	0	x
0	0	0	0	0	0	0	1	0	0	x
0	0	0	0	0	0	0	0	0	0	x
0	0	0	0	0	0	0	1	0	0	x
0	0	0	0	0	0	0	0	0	0	x
0	0	0	0	0	0	0	1	0	0	x
0	0	0	0	0	0	0	0	0	0	x
0	0	0	0	0	0	0	1	0	0	x
0	0	0	0	0	0	0	0	0	0	x
0	0	0	0	0	0	0	1	0	0	x
0	0	0	0	0	0	0	0	0	0	x
0	0	0	0	0	0	0	1	0	0	x
0	0	0	0	0	0	0	0	0	0	x
0	0	0	0	0	0	0	1	0	0	x
0	0	0	0	0	0	0	0	0	0	x
0	0	0	0	0	0	0	1	0	0	x
0	0	0	0	0	0	0	0	0	0	x
0	0	0	0	0	0	0	1	0	0	x
0	0	0	0	0	0	0	0	0	0	x
0	0	0	0	0	0	0	1	0	0	x
0	0	0	0	0	0	0	0	0	0	x
0	0	0	0	0	0	0	1	0	0	x
0	0	0	0	0	0	0	0	0	0	x
0	0	0	0	0	0	0	1	0	0	x
0	0	0	0	0	0	0	0	0	0	x
0	0	0	0	0	0	0	1	0	0	x
0	0	0	0	0	0	0	0	0	0	x
0	0	0	0	0	0	0	1	0	0	x
0	0	0	0	0	0	0	0	0	0	x
0	0	0	0	0	0	0	1	0	0	x
0	0	0	0	0	0	0	0	0	0	x
0	0	0	0	0	0	0	1	0	0	x
0	0	0	0	0	0	0	0	0	0	x
0	0	0	0	0	0	0	1	0	0	x
0	0	1792	0	1	0	0	0	0	0	x
0	0	1792	0	1	0	0	1	0	0	x
0	0	1536	0	1	0	0	0	0	0	x
0	0	1536	0	1	0	0	1	0	0	x
0	0	2817	0	1	0	0	0	0	0	x
0	0	2817	0	1	0	0	1	0	0	x
0	0	2048	0	1	0	0	0	0	0	x
0	0	2048	0	1	0	0	1	0	0	x
0	0	1536	0	1	0	0	0	0	0	x
0	0	1536	0	1	0	0	1	0	0	x
0	0	2818	0	1	0	0	0	0	0	x
0	0	2818	0	1	0	0	1	0	0	x
0	0	1024	0	1	0	0	0	0	0	x
0	0	1024	0	1	0	0	1	0	0	x
0	0	2561	0	1	0	0	0	0	0	x
0	0	2561	0	1	0	0	1	0	0	x
0	0	4864	0	1	0	0	0	0	0	x
0	0	4864	0	1	0	0	1	0	0	x
0	0	2819	0	1	0	0	0	0	0	x
0	0	2819	0	1	0	0	1	0	0	x
0	0	2561	0	1	0	0	0	0	0	x
0	0	2561	0	1	0	0	1	0	0	x
0	0	5120	0	1	0	0	0	0	0	x
0	0	5120	0	1	0	0	1	0	0	x
0	0	2820	0	1	0	0	0	0	0	x
0	0	2820	0	1	0	0	1	0	0	x
0	0	7936	0	1	0	0	0	0	0	x
0	0	7936	0	1	0	0	1	0	0	x
15	7	0	0	0	1	0	0	0	0	x
15	7	0	0	0	1	0	1	0	0	x
15	7	0	0	0	0	0	0	x	0	x
15	7	0	0	0	0	0	1	x	0	x
15	7	0	0	0	0	0	0	x	0	x
15	7	0	0	0	0	0	1	x	0	x
15	7	0	0	0	0	0	0	x	0	x
15	7	0	0	0	0	0	1	x	0	x
15	7	0	0	0	0	0	0	x	0	x
15	7	0	0	0	0	0	1	x	0	x
15	7	0	0	0	0	0	0	x	0	x
15	7	0	0	0	0	0	1	x	0	x
15	7	0	0	0	0	0	0	x	0	x
15	7	0	0	0	0	0	1	x	0	x
15	7	0	0	0	0	0	0	x	0	x
15	7	0	0	0	0	0	1	x	0	x
15	7	0	0	0	0	0	0	x	0	x
15	7	0	0	0	0	0	1	x	0	x
15	7	0	0	0	0	0	0	x	0	x
15	7	0	0	0	0	0	1	x	0	x
15	7	0	0	0	0	0	0	x	0	x
15	7	0	0	0	0	0	1	x	0	x
15	7	0	0	0	0	0	0	x	0	x
15	7	0	0	0	0	0	1	x	0	x
15	7	0	0	0	0	0	0	x	0	x
15	7	0	0	0	0	0	1	x	0	x
15	7	0	0	0	0	0	0	x	0	x
15	7	0	0	0	0	0	1	x	0	x
15	7	0	0	0	0	0	0	x	0	x
15	7	0	0	0	0	0	1	x	0	x
15	7	0	0	0	0	0	0	x	0	x
15	7	0	0	0	0	0	1	x	0	x
15	7	0	0	0	0	0	0	x	0	x
15	7	0	0	0	0	0	1	x	0	x
15	7	0	0	0	0	0	0	x	0	x
15	7	0	0	0	0	0	1	x	0	x
15	7	0	0	0	0	0	0	x	0	x
15	7	0	0	0	0	0	1	x	0	x
15	7	0	0	0	0	0	0	x	0	x
15	7	0	0	0	0	0	1	x	0	x
15	7	0	0	0	0	0	0	x	0	x
0	0	0	0	0	0	0	1	x	0	x
0	0	0	0	0	0	0	0	x	0	x
0	0	0	0	0	0	0	1	x	0	x
0	0	0	0	0	0	0	0	x	0	x
0	0	0	0	0	0	0	1	x	0	x
0	0	0	0	0	0	0	0	x	0	x
0	0	0	0	0	0	0	1	x	0	x
0	0	0	0	0	0	0	0	x	0	x
0	0	0	0	0	0	0	1	x	0	x
0	0	0	0	0	0	0	0	x	0	x
0	0	0	0	0	0	0	1	x	0	x
0	0	0	0	0	0	0	0	x	0	x
0	0	0	0	0	0	0	1	x	0	x
0	0	0	0	0	0	0	0	x	0	x
0	0	0	0	0	0	0	1	x	0	x
0	0	0	0	0	0	0	0	x	0	x
0	0	0	0	0	0	0	1	x	0	x
0	0	0	0	0	0	0	0	x	0	x
0	0	0	0	0	0	0	1	x	0	x
0	0	0	0	0	0	0	0	x	0	x
0	0	0	0	0	0	0	1	x	0	x
0	0	0	0	0	0	0	0	x	0	x
0	0	0	0	0	0	0	1	x	0	x
0	0	0	0	0	0	0	0	x	0	x
0	0	0	0	0	0	0	1	x	0	x
0	0	0	0	0	0	0	0	x	0	x
0	0	0	0	0	0	0	1	x	0	x
0	0	0	0	0	0	0	0	x	0	x
0	0	0	0	0	0	0	1	x	0	x
0	0	0	0	0	0	0	0	x	0	x
0	0	0	0	0	0	0	1	x	0	x
0	0	0	0	0	0	0	0	x	0	x
0	0	0	0	0	0	0	1	x	0	x
0	0	0	0	0	0	0	0	x	0	x
0	0	0	0	0	0	0	1	x	0	x
0	0	0	0	0	0	0	0	x	0	x
0	0	0	0	0	0	0	1	x	0	x
0	0	0	0	0	0	0	0	x	0	x
0	0	0	0	0	0	0	1	x	0	x
0	0	0	0	0	0	0	0	x	0	x
0	0	0	0	0	0	0	1	x	0	x
0	0	0	0	0	0	0	0	x	0	x
0	0	0	0	0	0	0	1	x	0	x
0	0	0	0	0	0	0	0	x	0	x
0	0	0	0	0	0	0	1	1	0	x
0	0	0	0	0	0	1	0	1	0	0
0	0	0	0	0	0	1	1	1	0	0
0	0	0	0	0	0	0	0	1	0	0
0	0	0	0	0	0	0	1	1	0	15
0	0	0	0	0	0	0	0	1	0	15
0	0	0	0	0	0	0	1	1	0	7
0	0	0	0	0	0	0	0	1	0	7
0	0	0	0	0	0	0	1	1	0	105
0	0	0	0	0	0	0	0	1	0	105
0	0	0	0	0	0	0	1	1	0	2
0	0	0	0	0	0	0	0	1	0	2
0	0	0	0	0	0	0	1	1	0	0
0	0	0	0	0	0	0	0	1	0	0
0	0	0	0	0	0	0	1	1	0	0
0	0	0	0	0	0	0	0	1	0	0
0	0	0	0	0	0	0	1	1	0	0
0	0	0	0	0	0	0	0	1	0	0
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*/

/* Test case LCD:
M	N	progIN	reset	progLoad	start	result	clk	valid	done	output
0	0	0	0	0	0	0	0	x	x	x
0	0	0	0	0	0	0	1	x	x	x
0	0	0	1	0	0	0	0	x	x	x
0	0	0	1	0	0	0	1	0	0	x
0	0	0	0	0	0	0	0	0	0	x
0	0	0	0	0	0	0	1	0	0	x
0	0	0	0	0	0	0	0	0	0	x
0	0	0	0	0	0	0	1	0	0	x
0	0	0	0	0	0	0	0	0	0	x
0	0	0	0	0	0	0	1	0	0	x
0	0	0	0	0	0	0	0	0	0	x
0	0	0	0	0	0	0	1	0	0	x
0	0	0	0	0	0	0	0	0	0	x
0	0	0	0	0	0	0	1	0	0	x
0	0	0	0	0	0	0	0	0	0	x
0	0	0	0	0	0	0	1	0	0	x
0	0	0	0	0	0	0	0	0	0	x
0	0	0	0	0	0	0	1	0	0	x
0	0	0	0	0	0	0	0	0	0	x
0	0	0	0	0	0	0	1	0	0	x
0	0	0	0	0	0	0	0	0	0	x
0	0	0	0	0	0	0	1	0	0	x
0	0	0	0	0	0	0	0	0	0	x
0	0	0	0	0	0	0	1	0	0	x
0	0	0	0	0	0	0	0	0	0	x
0	0	0	0	0	0	0	1	0	0	x
0	0	0	0	0	0	0	0	0	0	x
0	0	0	0	0	0	0	1	0	0	x
0	0	0	0	0	0	0	0	0	0	x
0	0	0	0	0	0	0	1	0	0	x
0	0	0	0	0	0	0	0	0	0	x
0	0	0	0	0	0	0	1	0	0	x
0	0	0	0	0	0	0	0	0	0	x
0	0	0	0	0	0	0	1	0	0	x
0	0	0	0	0	0	0	0	0	0	x
0	0	0	0	0	0	0	1	0	0	x
0	0	0	0	0	0	0	0	0	0	x
0	0	0	0	0	0	0	1	0	0	x
0	0	0	0	0	0	0	0	0	0	x
0	0	0	0	0	0	0	1	0	0	x
0	0	0	0	0	0	0	0	0	0	x
0	0	0	0	0	0	0	1	0	0	x
0	0	276	0	1	0	0	0	0	0	x
0	0	276	0	1	0	0	1	0	0	x
0	0	2816	0	1	0	0	0	0	0	x
0	0	2816	0	1	0	0	1	0	0	x
0	0	286	0	1	0	0	0	0	0	x
0	0	286	0	1	0	0	1	0	0	x
0	0	2821	0	1	0	0	0	0	0	x
0	0	2821	0	1	0	0	1	0	0	x
0	0	7685	0	1	0	0	0	0	0	x
0	0	7685	0	1	0	0	1	0	0	x
0	0	7936	0	1	0	0	0	0	0	x
0	0	7936	0	1	0	0	1	0	0	x
0	0	0	0	0	0	0	0	0	0	x
0	0	0	0	0	0	0	1	0	0	x
0	0	0	0	0	0	0	0	0	0	x
0	0	0	0	0	0	0	1	0	0	x
0	0	0	0	0	0	0	0	0	0	x
0	0	0	0	0	0	0	1	0	0	x
0	0	0	0	0	1	0	0	x	0	x
0	0	0	0	0	1	0	1	x	0	x
0	0	0	0	0	0	0	0	x	0	x
0	0	0	0	0	0	0	1	x	0	x
0	0	0	0	0	0	0	0	x	0	x
0	0	0	0	0	0	0	1	x	0	x
0	0	0	0	0	0	0	0	x	0	x
0	0	0	0	0	0	0	1	x	0	x
0	0	0	0	0	0	0	0	x	0	x
0	0	0	0	0	0	0	1	x	0	x
0	0	0	0	0	0	0	0	x	0	x
0	0	0	0	0	0	0	1	x	0	x
0	0	0	0	0	0	0	0	x	0	x
0	0	0	0	0	0	0	1	x	0	x
0	0	0	0	0	0	0	0	x	0	x
0	0	0	0	0	0	0	1	x	0	x
0	0	0	0	0	0	0	0	x	0	x
0	0	0	0	0	0	0	1	x	0	x
0	0	0	0	0	0	0	0	x	0	x
0	0	0	0	0	0	0	1	x	0	x
0	0	0	0	0	0	0	0	x	0	x
0	0	0	0	0	0	0	1	x	0	x
0	0	0	0	0	0	0	0	x	0	x
0	0	0	0	0	0	0	1	x	0	x
0	0	0	0	0	0	0	0	x	0	x
0	0	0	0	0	0	0	1	x	0	x
0	0	0	0	0	0	0	0	x	0	x
0	0	0	0	0	0	0	1	x	0	x
0	0	0	0	0	0	0	0	x	0	x
0	0	0	0	0	0	0	1	x	0	x
0	0	0	0	0	0	0	0	x	0	x
0	0	0	0	0	0	0	1	x	0	x
0	0	0	0	0	0	0	0	x	0	x
0	0	0	0	0	0	0	1	x	0	x
0	0	0	0	0	0	0	0	x	0	x
0	0	0	0	0	0	0	1	x	0	x
0	0	0	0	0	0	0	0	x	0	x
0	0	0	0	0	0	0	1	x	0	x
0	0	0	0	0	0	0	0	x	0	x
0	0	0	0	0	0	0	1	x	0	x
0	0	0	0	0	0	0	0	x	0	x
0	0	0	0	0	0	0	1	x	0	x
0	0	0	0	0	0	0	0	x	0	x
0	0	0	0	0	0	0	1	x	0	x
0	0	0	0	0	0	0	0	x	0	x
0	0	0	0	0	0	0	1	x	0	x
0	0	0	0	0	0	0	0	x	0	x
0	0	0	0	0	0	0	1	x	0	x
0	0	0	0	0	0	0	0	x	0	x
0	0	0	0	0	0	0	1	x	0	x
0	0	0	0	0	0	0	0	x	0	x
0	0	0	0	0	0	0	1	x	0	x
0	0	0	0	0	0	0	0	x	0	x
0	0	0	0	0	0	0	1	x	0	x
0	0	0	0	0	0	0	0	x	0	x
0	0	0	0	0	0	0	1	x	0	x
0	0	0	0	0	0	0	0	x	0	x
0	0	0	0	0	0	0	1	x	0	x
0	0	0	0	0	0	0	0	x	0	x
0	0	0	0	0	0	0	1	x	0	x
0	0	0	0	0	0	0	0	x	0	x
0	0	0	0	0	0	0	1	x	0	x
0	0	0	0	0	0	0	0	x	0	x
0	0	0	0	0	0	0	1	x	0	x
0	0	0	0	0	0	0	0	x	0	x
0	0	0	0	0	0	0	1	x	0	x
0	0	0	0	0	0	0	0	x	0	x
0	0	0	0	0	0	0	1	x	0	x
0	0	0	0	0	0	0	0	x	0	x
0	0	0	0	0	0	0	1	x	0	x
0	0	0	0	0	0	0	0	x	0	x
0	0	0	0	0	0	0	1	x	0	x
0	0	0	0	0	0	0	0	x	0	x
0	0	0	0	0	0	0	1	x	0	x
0	0	0	0	0	0	0	0	x	0	x
0	0	0	0	0	0	0	1	x	0	x
0	0	0	0	0	0	0	0	x	0	x
0	0	0	0	0	0	0	1	x	0	x
0	0	0	0	0	0	0	0	x	0	x
0	0	0	0	0	0	0	1	x	0	x
0	0	0	0	0	0	0	0	x	0	x
0	0	0	0	0	0	0	1	x	0	x
0	0	0	0	0	0	0	0	x	0	x
0	0	0	0	0	0	0	1	x	0	x
0	0	0	0	0	0	0	0	x	0	x
0	0	0	0	0	0	0	1	x	0	x
0	0	0	0	0	0	0	0	x	0	x
0	0	0	0	0	0	0	1	x	0	x
0	0	0	0	0	0	0	0	x	0	x
0	0	0	0	0	0	0	1	x	0	x
0	0	0	0	0	0	0	0	x	0	x
0	0	0	0	0	0	0	1	x	0	x
0	0	0	0	0	0	0	0	x	0	x
0	0	0	0	0	0	0	1	x	0	x
0	0	0	0	0	0	0	0	x	0	x
0	0	0	0	0	0	0	1	x	0	x
0	0	0	0	0	0	0	0	x	0	x
0	0	0	0	0	0	0	1	x	0	x
0	0	0	0	0	0	0	0	x	0	x
0	0	0	0	0	0	0	1	x	0	x
0	0	0	0	0	0	0	0	x	0	x
0	0	0	0	0	0	0	1	x	0	x
0	0	0	0	0	0	0	0	x	0	x
0	0	0	0	0	0	0	1	x	0	x
0	0	0	0	0	0	0	0	x	0	x
0	0	0	0	0	0	0	1	x	0	x
0	0	0	0	0	0	0	0	x	0	x
0	0	0	0	0	0	0	1	x	0	x
0	0	0	0	0	0	0	0	x	0	x
0	0	0	0	0	0	0	1	x	0	x
0	0	0	0	0	0	0	0	x	0	x
0	0	0	0	0	0	0	1	x	0	x
0	0	0	0	0	0	0	0	x	0	x
0	0	0	0	0	0	0	1	x	0	x
0	0	0	0	0	0	0	0	x	0	x
0	0	0	0	0	0	0	1	x	0	x
0	0	0	0	0	0	0	0	x	0	x
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*/

/* Test case LCD02:
M	N	progIN	reset	progLoad	start	result	clk	valid	done	output
0	0	0	0	0	0	0	0	x	x	x
0	0	0	0	0	0	0	1	x	x	x
0	0	0	1	0	0	0	0	x	x	x
0	0	0	1	0	0	0	1	0	0	x
0	0	0	0	0	0	0	0	0	0	x
0	0	0	0	0	0	0	1	0	0	x
0	0	0	0	0	0	0	0	0	0	x
0	0	0	0	0	0	0	1	0	0	x
0	0	0	0	0	0	0	0	0	0	x
0	0	0	0	0	0	0	1	0	0	x
0	0	0	0	0	0	0	0	0	0	x
0	0	0	0	0	0	0	1	0	0	x
0	0	0	0	0	0	0	0	0	0	x
0	0	0	0	0	0	0	1	0	0	x
0	0	0	0	0	0	0	0	0	0	x
0	0	0	0	0	0	0	1	0	0	x
0	0	0	0	0	0	0	0	0	0	x
0	0	0	0	0	0	0	1	0	0	x
0	0	0	0	0	0	0	0	0	0	x
0	0	0	0	0	0	0	1	0	0	x
0	0	0	0	0	0	0	0	0	0	x
0	0	0	0	0	0	0	1	0	0	x
0	0	0	0	0	0	0	0	0	0	x
0	0	0	0	0	0	0	1	0	0	x
0	0	0	0	0	0	0	0	0	0	x
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*/

/* Test case TC7:
M	N	progIN	reset	progLoad	start	result	clk	valid	done	output
0	0	0	0	0	0	0	0	x	x	x
0	0	0	0	0	0	0	1	x	x	x
0	0	0	1	0	0	0	0	x	x	x
0	0	0	1	0	0	0	1	0	0	0
0	0	0	0	0	0	0	0	0	0	0
0	0	0	0	0	0	0	1	0	0	0
0	0	0	0	0	0	0	0	0	0	0
0	0	0	0	0	0	0	1	0	0	0
0	0	0	0	0	0	0	0	0	0	0
0	0	0	0	0	0	0	1	0	0	0
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*/

/* Test case TC8:
M	N	progIN	reset	progLoad	start	result	clk	valid	done	output
0	0	0	0	0	0	0	0	x	x	x
0	0	0	0	0	0	0	1	x	x	x
0	0	0	1	0	0	0	0	x	x	x
0	0	0	1	0	0	0	1	0	0	0
0	0	0	0	0	0	0	0	0	0	0
0	0	0	0	0	0	0	1	0	0	0
0	0	0	0	0	0	0	0	0	0	0
0	0	0	0	0	0	0	1	0	0	0
0	0	0	0	0	0	0	0	0	0	0
0	0	0	0	0	0	0	1	0	0	0
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*/

/* Test case 02_P01T02:
M N progIN reset progLoad start result clk valid done output
0 0 0 0 0 0 0 0 x x x
0 0 0 0 0 0 0 1 x x x
0 0 0 1 0 0 0 0 x x x
0 0 0 1 0 0 0 1 0 0 0
0 0 0 0 0 0 0 0 0 0 0
0 0 0 0 0 0 0 1 0 0 0
0 0 0 0 0 0 0 0 0 0 0
0 0 0 0 0 0 0 1 0 0 0
0 0 0 0 0 0 0 0 0 0 0
0 0 0 0 0 0 0 1 0 0 0
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*/

/* Test case 02_jump:
M	N	progIN	reset	progLoad	start	result	clk	valid	done	output
0	0	0	0	0	0	0	0	x	x	x
0	0	0	0	0	0	0	1	x	x	x
0	0	0	1	0	0	0	0	x	x	x
0	0	0	1	0	0	0	1	0	0	0
0	0	0	0	0	0	0	0	0	0	0
0	0	0	0	0	0	0	1	0	0	0
0	0	0	0	0	0	0	0	0	0	0
0	0	0	0	0	0	0	1	0	0	0
0	0	0	0	0	0	0	0	0	0	0
0	0	0	0	0	0	0	1	0	0	0
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*/

/* Test case 03_triplejump:
M	N	progIN	reset	progLoad	start	result	clk	valid	done	output
0	0	0	0	0	0	0	0	x	x	x
0	0	0	0	0	0	0	1	x	x	x
0	0	0	1	0	0	0	0	x	x	x
0	0	0	1	0	0	0	1	0	0	0
0	0	0	0	0	0	0	0	0	0	0
0	0	0	0	0	0	0	1	0	0	0
0	0	0	0	0	0	0	0	0	0	0
0	0	0	0	0	0	0	1	0	0	0
0	0	0	0	0	0	0	0	0	0	0
0	0	0	0	0	0	0	1	0	0	0
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*/

/* Test case 04_pRamLoad:
M	N	progIN	reset	progLoad	start	result	clk	valid	done	output
0	0	0	0	0	0	0	0	x	x	x
0	0	0	0	0	0	0	1	x	x	x
0	0	0	1	0	0	0	0	x	x	x
0	0	0	1	0	0	0	1	0	0	0
0	0	0	0	0	0	0	0	0	0	0
0	0	0	0	0	0	0	1	0	0	0
0	0	0	0	0	0	0	0	0	0	0
0	0	0	0	0	0	0	1	0	0	0
0	0	0	0	0	0	0	0	0	0	0
0	0	0	0	0	0	0	1	0	0	0
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*/

/* Test case 05_primetest:
M	N	progIN	reset	progLoad	start	result	clk	valid	done	output
0	0	0	0	0	0	0	0	x	x	x
0	0	0	0	0	0	0	1	x	x	x
0	0	0	1	0	0	0	0	x	x	x
0	0	0	1	0	0	0	1	0	0	0
0	0	0	0	0	0	0	0	0	0	0
0	0	0	0	0	0	0	1	0	0	0
0	0	0	0	0	0	0	0	0	0	0
0	0	0	0	0	0	0	1	0	0	0
0	0	0	0	0	0	0	0	0	0	0
0	0	0	0	0	0	0	1	0	0	0
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*/

/* Test case 06_primetest+jump:
M	N	progIN	reset	progLoad	start	result	clk	valid	done	output
0	0	0	0	0	0	0	0	0	0	0
0	0	0	0	0	0	0	1	0	0	0
0	0	0	1	0	0	0	0	0	0	0
0	0	0	1	0	0	0	1	0	0	0
0	0	0	0	0	0	0	0	0	0	0
0	0	0	0	0	0	0	1	0	0	0
0	0	0	0	0	0	0	0	0	0	0
0	0	0	0	0	0	0	1	0	0	0
0	0	0	0	0	0	0	0	0	0	0
0	0	0	0	0	0	0	1	0	0	0
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*/

/* Test case Reset Again:
M	N	progIN	reset	progLoad	start	result	clk	valid	done	output
0	0	0	0	0	0	0	0	x	x	x
0	0	0	0	0	0	0	1	x	x	x
0	0	0	1	0	0	0	0	x	x	x
0	0	0	1	0	0	0	1	0	0	x
0	0	0	0	0	0	0	0	0	0	x
0	0	0	0	0	0	0	1	0	0	x
0	0	0	0	0	0	0	0	0	0	x
0	0	0	0	0	0	0	1	0	0	x
0	0	0	0	0	0	0	0	0	0	x
0	0	0	0	0	0	0	1	0	0	x
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*/

/* Test case 03_P02T01:
M N progIN reset progLoad start result clk valid done output
0 0 0 0 0 0 0 0 x x x
0 0 0 0 0 0 0 1 x x x
0 0 0 1 0 0 0 0 x x x
0 0 0 1 0 0 0 1 0 0 0
0 0 0 0 0 0 0 0 0 0 0
0 0 0 0 0 0 0 1 0 0 0
0 0 0 0 0 0 0 0 0 0 0
0 0 0 0 0 0 0 1 0 0 0
0 0 0 0 0 0 0 0 0 0 0
0 0 0 0 0 0 0 1 0 0 0
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*/

/* Test case Factorial:
M N progIN reset progLoad start result clk valid done output
0 0 0 0 0 0 0 0 x x x
0 0 0 0 0 0 0 1 x x x
0 0 0 1 0 0 0 0 0 0 0
0 0 0 1 0 0 0 1 0 0 0
0 0 0 0 0 0 0 0 0 0 0
0 0 0 0 0 0 0 1 0 0 0
0 0 0 0 0 0 0 0 0 0 0
0 0 0 0 0 0 0 1 0 0 0
0 0 0 0 0 0 0 0 0 0 0
0 0 0 0 0 0 0 1 0 0 0
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*/

/* Test case TC3:
M	N	progIN	reset	progLoad	start	result	clk	valid	done	output
0	0	0	0	0	0	0	0	x	x	x
0	0	0	0	0	0	0	1	x	x	x
0	0	0	1	0	0	0	0	x	x	x
0	0	0	1	0	0	0	1	0	0	0
0	0	0	0	0	0	0	0	0	0	0
0	0	0	0	0	0	0	1	0	0	0
0	0	0	0	0	0	0	0	0	0	0
0	0	0	0	0	0	0	1	0	0	0
0	0	0	0	0	0	0	0	0	0	0
0	0	0	0	0	0	0	1	0	0	0
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*/

/* Test case TC5:
M	N	progIN	reset	progLoad	start	result	clk	valid	done	output
0	0	0	0	0	0	0	0	x	x	x
0	0	0	0	0	0	0	1	x	x	x
0	0	0	1	0	0	0	0	x	x	x
0	0	0	1	0	0	0	1	0	0	0
0	0	0	0	0	0	0	0	0	0	0
0	0	0	0	0	0	0	1	0	0	0
0	0	0	0	0	0	0	0	0	0	0
0	0	0	0	0	0	0	1	0	0	0
0	0	0	0	0	0	0	0	0	0	0
0	0	0	0	0	0	0	1	0	0	0
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*/

/* Test case TC6:
M	N	progIN	reset	progLoad	start	result	clk	valid	done	output
0	0	0	0	0	0	0	0	x	x	x
0	0	0	0	0	0	0	1	x	x	x
0	0	0	1	0	0	0	0	x	x	x
0	0	0	1	0	0	0	1	0	0	0
0	0	0	0	0	0	0	0	0	0	0
0	0	0	0	0	0	0	1	0	0	0
0	0	0	0	0	0	0	0	0	0	0
0	0	0	0	0	0	0	1	0	0	0
0	0	0	0	0	0	0	0	0	0	0
0	0	0	0	0	0	0	1	0	0	0
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*/

/* Test case 08_exponent:
M	N	progIN	reset	progLoad	start	result	clk	valid	done	output
0	0	0	0	0	0	0	0	0	0	0
0	0	0	0	0	0	0	1	0	0	0
0	0	0	1	0	0	0	0	0	0	0
0	0	0	1	0	0	0	1	0	0	0
0	0	0	0	0	0	0	0	0	0	0
0	0	0	0	0	0	0	1	0	0	0
0	0	0	0	0	0	0	0	0	0	0
0	0	0	0	0	0	0	1	0	0	0
0	0	0	0	0	0	0	0	0	0	0
0	0	0	0	0	0	0	1	0	0	0
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*/
