// Digital circuit 04_Solution.dig as structural Verilog
module _04_Solution (
  input  C1,
  input  C2,
  output Z
);

  and and_1 (Z, C1, C2);

  // Notes on the sheet:
  //   C1: Hz: 10
  //   C2: Hz: 10
endmodule
