// Digital circuit 01_XOR_(Sum_of_Products).dig as structural Verilog
module _01_XOR__Sum_of_Products (
  input  A,
  input  B,
  output Output
);

  wire and_1_out, and_2_out, not_1_out, not_2_out;

  not not_1 (not_1_out, A);
  not not_2 (not_2_out, B);
  and and_1 (and_1_out, A, not_2_out);
  and and_2 (and_2_out, not_1_out, B);
  or or_1 (Output, and_1_out, and_2_out);
endmodule
