// Digital circuit 05.dig as structural Verilog
module _05 (
  input  A,
  input  B,
  input  C,
  input  D,
  output Z1,
  output Z2,
  output Z3
);

  wire and_1_out, and_2_out, and_3_out, and_4_out, and_5_out, and_6_out, not_1_out, not_2_out, not_3_out,
       not_4_out, xnor_1_out, xnor_2_out;

  not not_1 (not_1_out, A);
  not not_2 (not_2_out, B);
  not not_3 (not_3_out, C);
  not not_4 (not_4_out, D);
  and and_1 (and_1_out, A, not_3_out);
  and and_2 (and_2_out, B, not_3_out, not_4_out);
  and and_3 (and_3_out, A, B, not_4_out);
  xnor xnor_1 (xnor_1_out, A, C);
  xnor xnor_2 (xnor_2_out, B, D);
  and and_4 (and_4_out, C, A);
  and and_5 (and_5_out, C, D, not_2_out);
  and and_6 (and_6_out, D, not_1_out, not_2_out);
  or or_1 (Z1, and_1_out, and_2_out, and_3_out);
  or or_2 (Z2, xnor_1_out, xnor_2_out);
  or or_3 (Z3, and_4_out, and_5_out, and_6_out);
endmodule
