// Digital circuit Template-01.dig as structural Verilog
module Template_01 (
  input  [3:0] In,
  output A,
  output B,
  output C,
  output D,
  output E,
  output F,
  output G,
  output H
);

  wire and_1_out, and_2_out, and_3_out, and_4_out, and_5_out, and_6_out, and_7_out, and_8_out, and_9_out,
       and_10_out, and_11_out, and_12_out, and_13_out, and_14_out, and_15_out, and_16_out, and_17_out,
       and_18_out, and_19_out, and_20_out, and_21_out, and_22_out, not_1_out, not_2_out, not_3_out,
       not_4_out, or_1_out, or_2_out, or_3_out, or_4_out, or_5_out, or_6_out, xor_1_out;

  not not_1 (not_1_out, In[3]);
  not not_2 (not_2_out, In[2]);
  not not_3 (not_3_out, In[1]);
  not not_4 (not_4_out, In[0]);
  xor xor_1 (xor_1_out, In[2], In[0]);
  and and_1 (and_1_out, In[2], In[1], not_4_out);
  and and_2 (and_2_out, In[2], not_3_out, In[0]);
  and and_3 (and_3_out, In[3], In[1]);
  and and_4 (and_4_out, In[3], In[2]);
  and and_5 (and_5_out, not_2_out, In[1], not_4_out);
  and and_6 (and_6_out, In[3], In[1]);
  and and_7 (and_7_out, In[3], In[2]);
  and and_8 (and_8_out, not_1_out, not_2_out, not_3_out, In[0]);
  and and_9 (and_9_out, In[2], not_3_out, not_4_out);
  and and_10 (and_10_out, In[2], In[1], In[0]);
  and and_11 (and_11_out, In[3], In[1]);
  and and_12 (and_12_out, In[3], In[2]);
  and and_13 (and_13_out, In[2], not_3_out, not_4_out);
  and and_14 (and_14_out, In[3], In[1]);
  and and_15 (and_15_out, not_1_out, not_2_out, not_3_out, In[0]);
  and and_16 (and_16_out, not_2_out, In[1]);
  and and_17 (and_17_out, In[3], In[2]);
  and and_18 (and_18_out, not_1_out, not_2_out, not_3_out);
  and and_19 (and_19_out, In[2], In[1], In[0]);
  and and_20 (and_20_out, In[3], In[1]);
  and and_21 (and_21_out, In[3], In[2]);
  and and_22 (and_22_out, not_3_out, not_1_out, xor_1_out);
  or or_1 (or_1_out, and_1_out, and_2_out, and_3_out, and_4_out);
  or or_2 (or_2_out, and_5_out, and_6_out, and_7_out);
  or or_3 (or_3_out, and_8_out, and_9_out, and_10_out, and_11_out, and_12_out);
  or or_4 (or_4_out, and_13_out, and_14_out, In[0]);
  or or_5 (or_5_out, and_15_out, and_16_out, and_17_out);
  or or_6 (or_6_out, and_18_out, and_19_out, and_20_out, and_21_out);
  not not_5 (A, and_22_out);
  not not_6 (B, or_1_out);
  not not_7 (C, or_2_out);
  not not_8 (D, or_3_out);
  not not_9 (E, or_4_out);
  not not_10 (F, or_5_out);
  not not_11 (G, or_6_out);
  // NotConnected on H
  Seven_Seg seven_seg_1 (.a(A), .b(B), .c(C), .d(D), .e(E), .f(F), .g(G), .dp(H));
endmodule
