// Digital circuit Template-03.dig as structural Verilog
module Template_03 (
  input  [3:0] In,
  input  [1:0] Selector,
  output [3:0] Output
);

  wire decoder_1_out_0, decoder_1_out_1, decoder_1_out_2, decoder_1_out_3;

  Decoder #(.Selector_Bits(2)) decoder_1 (
    .sel(Selector), .out_0(decoder_1_out_0), .out_1(decoder_1_out_1), .out_2(decoder_1_out_2),
    .out_3(decoder_1_out_3));
  ROM #(.AddrBits(4), .Bits(4)) Excess (.A(In), .sel(decoder_1_out_0), .D(Output));
  ROM #(.AddrBits(4), .Bits(4)) Cyclic (.A(In), .sel(decoder_1_out_1), .D(Output));
  ROM #(.AddrBits(4), .Bits(4)) _2_4_2_1_code (.A(In), .sel(decoder_1_out_2), .D(Output));
  ROM #(.AddrBits(4), .Bits(4)) _6_4_2__3_code (.A(In), .sel(decoder_1_out_3), .D(Output));

  // Notes on the sheet:
  //   contents of Excess (hex, n*v repeats v):
  //   3,4,5,6,7,8,9,a,b,c
  //   contents of Cyclic (hex, n*v repeats v):
  //   0,1,3,2,6,7,5,4,c,d
  //   contents of _2_4_2_1_code (hex, n*v repeats v):
  //   0,1,2,3,4,b,c,d,e,f
  //   contents of _6_4_2__3_code (hex, n*v repeats v):
  //   0,5,2,9,4,b,6,d,a,f
endmodule
