// Digital circuit Template-04.dig as structural Verilog
module Template_04 (
  input  [6:0] In,
  output [6:0] Output
);

  wire [2:0] xor_2_out;
  wire [6:0] demultiplexer_1_out_1;

  xor xor_1 (xor_2_out[0], In[6], In[4], In[2], In[0]);
  xor xor_2 (xor_2_out[1], In[5], In[4], In[1], In[0]);
  xor xor_3 (xor_2_out[2], In[0], In[1], In[2], In[3]);
  Demultiplexer #(.Selector_Bits(3)) demultiplexer_1 (
    .sel(xor_2_out), .in(1'b1), .out_1(demultiplexer_1_out_1[6]), .out_2(demultiplexer_1_out_1[5]),
    .out_3(demultiplexer_1_out_1[4]), .out_4(demultiplexer_1_out_1[3]), .out_5(demultiplexer_1_out_1[2]),
    .out_6(demultiplexer_1_out_1[1]), .out_7(demultiplexer_1_out_1[0]));  // open: out_0
  assign Output = In ^ demultiplexer_1_out_1;  // XOr xor_4, 7 bits wide
endmodule
