// Digital circuit Template.dig as structural Verilog
module Template (
  input  T,
  input  Clear,
  input  Clock,
  output Q,
  output Q_2
);

  wire nand_1_out, nand_2_out, nand_3_out, nand_4_out, or_1_out, xor_1_out;

  xor xor_1 (xor_1_out, T, Q_2);
  nand nand_1 (nand_1_out, nand_4_out, nand_2_out);
  nand nand_2 (nand_2_out, or_1_out, Clock);
  nand nand_3 (nand_3_out, nand_2_out, Clock, nand_4_out);
  nand nand_4 (nand_4_out, nand_3_out, xor_1_out);
  or or_1 (or_1_out, nand_1_out, Clear);
  nand nand_5 (Q_2, nand_2_out, Q);
  nand nand_6 (Q, Q_2, nand_3_out);
endmodule
