// Digital circuit Lab7.dig as structural Verilog
module Lab7 (
  input  reset,
  input  clk,
  output A,
  output B,
  output C
);

  wire A_t, and_1_out, and_2_out, and_3_out, and_4_out, and_5_out, and_6_out, and_7_out, and_8_out, B_t, C_t,
       or_1_out, or_2_out, or_3_out;

  and and_1 (and_1_out, B_t, C_t);
  and and_2 (and_2_out, B, C);
  or or_1 (or_1_out, and_1_out, and_2_out);
  D_FF_AS d_ff_as_1 (.Set(1'b0), .D(or_1_out), .C(clk), .Clr(reset), .Q(A), .nQ(A_t));
  and and_3 (and_3_out, A, C_t);
  and and_4 (and_4_out, B, C_t);
  and and_5 (and_5_out, A_t, B);
  or or_2 (or_2_out, and_3_out, and_4_out, and_5_out);
  D_FF_AS d_ff_as_2 (.Set(1'b0), .D(or_2_out), .C(clk), .Clr(reset), .Q(B), .nQ(B_t));
  and and_6 (and_6_out, A_t, B);
  and and_7 (and_7_out, B, C);
  and and_8 (and_8_out, A, C);
  or or_3 (or_3_out, and_6_out, and_7_out, and_8_out);
  D_FF_AS d_ff_as_3 (.Set(1'b0), .D(or_3_out), .C(clk), .Clr(reset), .Q(C), .nQ(C_t));
endmodule
