// Digital circuit Lab8-gcd.dig as structural Verilog
module Lab8_gcd (
  input  [7:0] A,
  input  [7:0] B,
  input  start,
  input  clk,
  input  clear,
  output [7:0] \output ,
  output busy
);

  wire A0, A1, A2, A3, and_1_out, and_2_out, and_3_out, and_4_out, clr, comparator_2_eq, comparator_2_gt,
       comparator_2_lt, M_eq_N, multiplexer_1_out, multiplexer_3_out, or_1_out, or_2_out, or_3_out, Qa;
  wire [0:0] Qa_plus_b;
  wire [7:0] M, multiplexer_2_out, multiplexer_4_out, N, sub_1_s, sub_2_s;

  not not_1 (clr, clear);
  Multiplexer #(.Selector_Bits(2)) multiplexer_1 (
    .sel({Qa, Qa_plus_b[0]}), .in_0(1'b0), .in_1(1'b1), .in_2(1'b0), .in_3(1'b0), .out(multiplexer_1_out));
  and and_1 (and_1_out, A2, comparator_2_gt);
  and and_2 (and_2_out, multiplexer_1_out, clr);
  Sub #(.Bits(8)) sub_1 (.a(M), .b(N), .c_i(1'b0), .s(sub_1_s));  // open: c_o
  or or_1 (or_1_out, start, and_1_out);
  D_FF d_ff_1 (.D(and_2_out), .C(clk), .Q(Qa));  // open: nQ
  Comparator #(.Bits(8)) comparator_1 (.a(M), .b(N), .eq(M_eq_N));  // open: gt, lt
  Comparator #(.Bits(8)) comparator_2 (.a(M), .b(N), .gt(comparator_2_gt), .eq(comparator_2_eq), .lt(comparator_2_lt));
  Multiplexer #(.Bits(8)) multiplexer_2 (.sel(comparator_2_gt), .in_0(A), .in_1(sub_1_s), .out(multiplexer_2_out));
  or or_2 (or_2_out, comparator_2_eq, comparator_2_lt);
  Register #(.Bits(8)) Load_M (.D(multiplexer_2_out), .C(clk), .en(or_1_out), .Q(M));
  Multiplexer #(.Selector_Bits(2)) multiplexer_3 (
    .sel({Qa, Qa_plus_b[0]}), .in_0(start), .in_1(M_eq_N), .in_2(1'b1), .in_3(1'b0), .out(multiplexer_3_out));
  and and_3 (and_3_out, A2, or_2_out);
  and and_4 (and_4_out, multiplexer_3_out, clr);
  Sub #(.Bits(8)) sub_2 (.a(N), .b(M), .c_i(1'b0), .s(sub_2_s));  // open: c_o
  or or_3 (or_3_out, start, and_3_out);
  D_FF d_ff_2 (.D(and_4_out), .C(clk), .Q(Qa_plus_b[0]));  // open: nQ
  Multiplexer #(.Bits(8)) multiplexer_4 (.sel(or_2_out), .in_0(B), .in_1(sub_2_s), .out(multiplexer_4_out));
  Decoder #(.Selector_Bits(2)) decoder_1 (.sel({Qa, Qa_plus_b[0]}), .out_0(A0), .out_1(A1), .out_2(A2), .out_3(A3));
  Register #(.Bits(8)) Load_N (.D(multiplexer_4_out), .C(clk), .en(or_3_out), .Q(N));
  or or_4 (busy, A1, A2);
  Register #(.Bits(8)) Load_Ans (.D(M), .C(clk), .en(A3), .Q(\output ));

  // Other names for the same wires on the sheet: Qa_plus_b[1] = Qa; Qb = Qa_plus_b[0]
endmodule

/* Test case:
A B start clear clk busy output
0xF 0x6 0 0 0 0 0
0xF 0x6 0 0 1 X 0
0xF 0x6 1 0 0 X 0
0xF 0x6 1 0 1 X 0
0xF 0x6 1 0 0 X 0
loop(x,1000)
0xF 0x6 0 0 1 X X
0xF 0x6 0 0 0 X X
end loop
0xF 0x6 0 0 0 0 0x3
*/
